// Logisim project ProyectoAC.circ as structural Verilog
module S_MIPS_Board (
  input  DESHABILITAR_DISPATCHER,
  output halt
);

  wire button_1_out, CLK, CS, d_ff_1_q, LCLR, LoadRAM, LoadRAMOn, LW, R_R_W, R_W, ram_dispatcher_1_finished,
       RCS, Reset_out, RST, TTY_EN;
  wire [2:0] KDB;
  wire [3:0] LMask, Mask, ram_1_read_time, ram_1_write_time, RMask;
  wire [6:0] KDB_DATA, TTY_DATA;
  wire [15:0] Addr, LAddr, RAddr;
  wire [31:0] I0, I1, I2, I3, LData, ram_1_data_out_0, ram_1_data_out_1, ram_1_data_out_2, ram_1_data_out_3,
       RI0, RI1, RI2, RI3;

  TTY #(.rows(25), .cols(80)) tty_1 (.data(TTY_DATA), .clk(CLK), .we(TTY_EN), .clr(RST));
  not not_1 (LoadRAMOn, ram_dispatcher_1_finished);
  RAM_Dispatcher ram_dispatcher_1 (
    .WriteTime(ram_1_write_time), .Clock(CLK), .Data(LData), .Address(LAddr), .Mask(LMask),
    .Finished(ram_dispatcher_1_finished), .Write(LW), .CLR(LCLR));
  Keyboard #(.buflen(64)) keyboard_1 (.clk(CLK), .re(KDB[0]), .avail(KDB[2]), .data(KDB_DATA));  // open: clr
  RAM ram_1 (
    .Address(RAddr), .Data_Out_0(ram_1_data_out_0), .Data_Out_1(ram_1_data_out_1),
    .Data_Out_2(ram_1_data_out_2), .Data_Out_3(ram_1_data_out_3), .Data_In_0(RI0), .Data_In_1(RI1),
    .Data_In_2(RI2), .Data_In_3(RI3), .Mask(RMask), .nRead_Write(R_R_W), .Chip_Select(RCS),
    .Read_Time(ram_1_read_time), .Reset(button_1_out), .Write_Time(ram_1_write_time));
  Button button_1 (.out(button_1_out));
  D_Flip_Flop d_ff_1 (.clk(CLK), .D(1'b1), .Q(d_ff_1_q), .reset(Reset_out));  // open: Qn, preset, en
  Button Reset (.out(Reset_out));
  S_MIPS s_mips_1 (
    .Kbd_Enable(KDB[0]), .Address(Addr), .Kbd_Clear(KDB[1]), .Kbd_Available(KDB[2]), .RAM_In_0(I0),
    .Kbd_ASCII_Data(KDB_DATA), .RAM_In_1(I1), .TTY_Enable(TTY_EN), .RAM_In_2(I2), .RAM_In_3(I3),
    .TTY_ASCII_Data(TTY_DATA), .Reset(RST), .RAM_Out_0(ram_1_data_out_0), .Clock(CLK),
    .RAM_Out_1(ram_1_data_out_1), .Stop(halt), .RAM_Out_2(ram_1_data_out_2), .RAM_Out_3(ram_1_data_out_3),
    .Mask(Mask), .Read_Time(ram_1_read_time), .Write_Time(ram_1_write_time), .nRead_Write(R_W),
    .Chip_Select(CS));
  D_Flip_Flop d_ff_2 (.clk(CLK), .D(d_ff_1_q), .Qn(LCLR), .reset(Reset_out));  // open: Q, preset, en
  or or_1 (RST, LCLR, LoadRAM);
  Clock clock_1 (.out(CLK));
  Multiplexer #(.width(32), .enable("false")) multiplexer_1 (.in0(I0), .in1(LData), .out(RI0), .sel(LoadRAM));
  Multiplexer #(.width(32), .enable("false")) multiplexer_2 (.in0(I1), .in1(LData), .out(RI1), .sel(LoadRAM));
  Multiplexer #(.width(32), .enable("false")) multiplexer_3 (.in0(I2), .in1(LData), .out(RI2), .sel(LoadRAM));
  Multiplexer #(.width(32), .enable("false")) multiplexer_4 (.in0(I3), .in1(LData), .out(RI3), .sel(LoadRAM));
  and and_1 (LoadRAM, ~DESHABILITAR_DISPATCHER, LoadRAMOn);  // AND_Gate
  Multiplexer #(.width(16), .enable("false")) multiplexer_5 (.in0(Addr), .in1(LAddr), .out(RAddr), .sel(LoadRAM));
  Multiplexer #(.width(4), .enable("false")) multiplexer_6 (.in0(Mask), .in1(LMask), .out(RMask), .sel(LoadRAM));
  Multiplexer #(.enable("false")) multiplexer_7 (.in0(CS), .in1(LW), .out(RCS), .sel(LoadRAM));
  Multiplexer #(.enable("false")) multiplexer_8 (.in0(R_W), .in1(LW), .out(R_R_W), .sel(LoadRAM));

  // Notes on the sheet:
  //   NO MODIFICAR
  //   Keyboard
endmodule

module RAM (
  input  [15:0] Address,
  input  [31:0] Data_In_0,
  input  [31:0] Data_In_1,
  input  [31:0] Data_In_2,
  input  [31:0] Data_In_3,
  input  [3:0] Mask,
  input  nRead_Write,
  input  Chip_Select,
  input  Reset,
  output [31:0] Data_Out_0,
  output [31:0] Data_Out_1,
  output [31:0] Data_Out_2,
  output [31:0] Data_Out_3,
  output [3:0] Read_Time,
  output [3:0] Write_Time
);

  wire and_2_out, and_3_out, and_4_out, and_5_out, and_6_out, and_7_out, and_8_out, and_9_out, Changed, CLK,
       comparator_2_eq, comparator_3_eq, comparator_4_eq, comparator_5_eq, comparator_6_eq, Count,
       demultiplexer_3_out0, Idle, Idle_q, Load, Load0, Load1, nand_1_out, or_1_out, or_2_out, or_3_out,
       or_4_out, or_5_out, or_6_out, or_7_out, or_8_out, or_9_out, or_10_out, Proc_q, Update_Mem, Zero_Time;
  wire [3:0] counter_1_q, multiplexer_1_out, subtractor_1_out;
  wire [31:0] register_1_q, register_2_q, register_3_q, register_4_q, register_5_q;

  // Probe on 4'b0011
  // Probe on 4'b0010
  Multiplexer #(.width(4), .enable("false")) multiplexer_1 (
    .in0(4'b0011), .in1(4'b0010), .out(multiplexer_1_out), .sel(nRead_Write));
  or or_1 (or_1_out, Idle, Update_Mem);
  or or_2 (or_2_out, ~Chip_Select, Reset);  // OR_Gate
  Subtractor #(.width(4)) subtractor_1 (.a(multiplexer_1_out), .b(4'b0010), .out(subtractor_1_out));  // open: bin, bout
  Demultiplexer #(.enable("false")) demultiplexer_1 (.out0(Idle), .out1(Load0), .in(Idle_q), .sel(Changed));
  D_Flip_Flop u_Idle (.clk(CLK), .D(or_1_out), .Q(Idle_q), .preset(or_2_out));  // open: Qn, en, reset
  // Probe on counter_1_q
  Counter #(.width(4), .max('hf)) counter_1 (
    .load(Load), .D(subtractor_1_out), .count(Count), .Q(counter_1_q), .clk(CLK), .clr(or_3_out));  // open: carry
  or or_3 (or_3_out, ~Chip_Select, Reset);  // OR_Gate
  Comparator #(.width(4), .mode("unsigned")) comparator_1 (
    .a(4'b0000), .b(counter_1_q), .eq(Zero_Time));  // open: gt, lt
  or or_4 (or_4_out, Count, Load0, Load1);
  Register #(.width(32)) register_1 (.D(Data_In_0), .en(Chip_Select), .Q(register_1_q), .clk(CLK), .clr(or_5_out));
  or or_5 (or_5_out, ~Chip_Select, Reset);  // OR_Gate
  Register #(.width(32)) register_2 (.D(Data_In_1), .en(Chip_Select), .Q(register_2_q), .clk(CLK), .clr(or_6_out));
  or or_6 (or_6_out, ~Chip_Select, Reset);  // OR_Gate
  Register #(.width(32)) register_3 (.D(Data_In_2), .en(Chip_Select), .Q(register_3_q), .clk(CLK), .clr(or_7_out));
  or or_7 (or_7_out, ~Chip_Select, Reset);  // OR_Gate
  Register #(.width(32)) register_4 (.D(Data_In_3), .en(Chip_Select), .Q(register_4_q), .clk(CLK), .clr(or_8_out));
  or or_8 (or_8_out, ~Chip_Select, Reset);  // OR_Gate
  Register #(.width(32)) register_5 (
    .D({{11{1'b1}}, nRead_Write, Mask, Address}), .en(Chip_Select), .Q(register_5_q), .clk(CLK),
    .clr(or_9_out));
  or or_9 (or_9_out, ~Chip_Select, Reset);  // OR_Gate
  D_Flip_Flop Proc (.clk(CLK), .D(or_4_out), .Q(Proc_q), .reset(or_10_out));  // open: Qn, preset, en
  or or_10 (or_10_out, ~Chip_Select, Reset);  // OR_Gate
  Demultiplexer #(.enable("false")) demultiplexer_2 (
    .out0(Count), .out1(Update_Mem), .in(demultiplexer_3_out0), .sel(Zero_Time));
  Demultiplexer #(.enable("false")) demultiplexer_3 (
    .out0(demultiplexer_3_out0), .out1(Load1), .in(Proc_q), .sel(Changed));
  Clock clock_1 (.out(CLK));
  Comparator #(.width(32)) comparator_2 (.a(register_1_q), .b(Data_In_0), .eq(comparator_2_eq));  // open: gt, lt
  Comparator #(.width(32)) comparator_3 (.a(register_2_q), .b(Data_In_1), .eq(comparator_3_eq));  // open: gt, lt
  Comparator #(.width(32)) comparator_4 (.a(register_3_q), .b(Data_In_2), .eq(comparator_4_eq));  // open: gt, lt
  Comparator #(.width(32)) comparator_5 (.a(register_4_q), .b(Data_In_3), .eq(comparator_5_eq));  // open: gt, lt
  Comparator #(.width(32)) comparator_6 (
    .a(register_5_q), .b({{11{1'b1}}, nRead_Write, Mask, Address}), .eq(comparator_6_eq));  // open: gt, lt
  nand nand_1 (nand_1_out, comparator_6_eq, comparator_2_eq, comparator_3_eq, comparator_4_eq, comparator_5_eq);
  and and_1 (Changed, nand_1_out, Chip_Select);
  or or_11 (Load, Count, Load1, Load0);
  and and_2 (and_2_out, Mask[0], Update_Mem, nRead_Write);
  and and_3 (and_3_out, Mask[1], Update_Mem, nRead_Write);
  and and_4 (and_4_out, Mask[2], Update_Mem, nRead_Write);
  and and_5 (and_5_out, Mask[3], Update_Mem, nRead_Write);
  RAM_part #(.addrWidth(16), .dataWidth(32), .bus("separate")) ram_1 (
    .addr(Address), .din(Data_In_0), .data(Data_Out_0), .str(and_2_out), .sel(Chip_Select), .clk(CLK),
    .ld(and_6_out), .clr(Reset));
  and and_6 (and_6_out, ~nRead_Write, Idle);  // AND_Gate
  RAM_part #(.addrWidth(16), .dataWidth(32), .bus("separate")) ram_2 (
    .addr(Address), .din(Data_In_1), .data(Data_Out_1), .str(and_3_out), .sel(Chip_Select), .clk(CLK),
    .ld(and_7_out), .clr(Reset));
  and and_7 (and_7_out, ~nRead_Write, Idle);  // AND_Gate
  RAM_part #(.addrWidth(16), .dataWidth(32), .bus("separate")) ram_3 (
    .addr(Address), .din(Data_In_2), .data(Data_Out_2), .str(and_4_out), .sel(Chip_Select), .clk(CLK),
    .ld(and_8_out), .clr(Reset));
  and and_8 (and_8_out, ~nRead_Write, Idle);  // AND_Gate
  RAM_part #(.addrWidth(16), .dataWidth(32), .bus("separate")) ram_4 (
    .addr(Address), .din(Data_In_3), .data(Data_Out_3), .str(and_5_out), .sel(Chip_Select), .clk(CLK),
    .ld(and_9_out), .clr(Reset));
  and and_9 (and_9_out, ~nRead_Write, Idle);  // AND_Gate

  assign Read_Time = 4'b0011;
  assign Write_Time = 4'b0010;

  // Other names for the same wires on the sheet: M0 = Mask[0]; M1 = Mask[1]; M2 = Mask[2]; M3 = Mask[3];
  //   RW = nRead_Write; CLR = Reset; CS = Chip_Select; Load2 = Count

  // Notes on the sheet:
  //   NO MODIFICAR
  //   excepto quizás los valores RT y WT
  //   BANK0
  //   BANK1
  //   BANK2
  //   BANK3
endmodule

module S_MIPS (
  input  Kbd_Available,
  input  [6:0] Kbd_ASCII_Data,
  input  [31:0] RAM_Out_0,
  input  [31:0] RAM_Out_1,
  input  Reset,
  input  [31:0] RAM_Out_2,
  input  Clock,
  input  [31:0] RAM_Out_3,
  input  [3:0] Read_Time,
  input  [3:0] Write_Time,
  output Kbd_Enable,
  output [15:0] Address,
  output Kbd_Clear,
  output TTY_Enable,
  output [6:0] TTY_ASCII_Data,
  output Stop,
  output [31:0] RAM_In_0,
  output [31:0] RAM_In_1,
  output [31:0] RAM_In_2,
  output [31:0] RAM_In_3,
  output [3:0] Mask,
  output nRead_Write,
  output Chip_Select
);


  // Other names for the same wires on the sheet: CLK = Clock; CLR = Reset; CS = Chip_Select;
  //   KBD_AVAIL = Kbd_Available; KBD_CLR = Kbd_Clear; KBD_DATA[6:0] = Kbd_ASCII_Data; RAM_A[15:0] = Address;
  //   RAM_INPUT_0[31:0] = RAM_In_0; RAM_INPUT_1[31:0] = RAM_In_1; RAM_INPUT_2[31:0] = RAM_In_2;
  //   RAM_INPUT_3[31:0] = RAM_In_3; RAM_MASK[3:0] = Mask; RAM_OUTPUT_0[31:0] = RAM_Out_0;
  //   RAM_OUTPUT_1[31:0] = RAM_Out_1; RAM_OUTPUT_2[31:0] = RAM_Out_2; RAM_OUTPUT_3[31:0] = RAM_Out_3;
  //   RW = nRead_Write; TTY_DATA[6:0] = TTY_ASCII_Data

  // Notes on the sheet:
  //   RAM ADDRESS
  //   DATA FROM RAM
  //   DATA TO RAM
  //   DATA WRITE MASK
  //   RAM TIMING
  //   RAM CONTROL
  //   KEYBOARD
  //   TTY
  //   SEQUENCING
endmodule

module RAM_Dispatcher (
  input  [3:0] WriteTime,
  input  Clock,
  input  CLR,
  output [31:0] Data,
  output [15:0] Address,
  output [3:0] Mask,
  output Finished,
  output Write
);

  wire demultiplexer_2_out1, demultiplexer_3_out1, End, IDLE_q, IncAddr, Load, or_1_out, or_2_out, While_q,
       WriteEnd;
  wire [3:0] counter_1_q;
  wire [31:0] CurrentAddress_q;

  Counter #(.width(32), .max('hffffffff)) CurrentAddress (
    .count(IncAddr), .Q({CurrentAddress_q[31:18], Address, CurrentAddress_q[1:0]}), .clk(Clock), .clr(CLR));  // open: load, D, carry
  or or_1 (or_1_out, IncAddr, demultiplexer_3_out1, Finished);
  D_Flip_Flop IDLE (.clk(Clock), .D(or_1_out), .Q(IDLE_q), .preset(CLR));  // open: Qn, en, reset
  Demultiplexer #(.enable("false")) demultiplexer_1 (.out0(Load), .out1(Finished), .in(IDLE_q), .sel(End));
  D_Flip_Flop While (.clk(Clock), .D(or_2_out), .Q(While_q), .reset(CLR));  // open: Qn, preset, en
  or or_2 (or_2_out, Write, Load);
  RAM_part #(.addrWidth(18), .dataWidth(32)) ram_1 (
    .addr({Address, CurrentAddress_q[1:0]}), .data(Data), .clk(Clock));  // open: sel, ld, clr
  Demultiplexer #(.enable("false")) demultiplexer_2 (
    .out0(Write), .out1(demultiplexer_2_out1), .in(While_q), .sel(WriteEnd));
  Decoder #(.select(2)) decoder_1 (
    .out0(Mask[0]), .out1(Mask[1]), .out2(Mask[2]), .out3(Mask[3]), .sel(CurrentAddress_q[1:0]));  // open: en
  Demultiplexer #(.enable("false")) demultiplexer_3 (
    .out0(IncAddr), .out1(demultiplexer_3_out1), .in(demultiplexer_2_out1), .sel(End));
  Counter #(.width(4), .max('hf)) counter_1 (
    .load(Load), .D(WriteTime), .count(Write), .Q(counter_1_q), .clk(Clock));  // open: carry, clr
  Comparator #(.width(32)) comparator_1 (.a(Data), .b({32{1'b1}}), .eq(End));  // open: gt, lt
  Comparator #(.width(4)) comparator_2 (.a(4'b0000), .b(counter_1_q), .eq(WriteEnd));  // open: gt, lt

  // Other names for the same wires on the sheet: CLK = Clock; Count = Write; WT[3:0] = WriteTime
endmodule

module ALU (
  input  [31:0] in_1,
  input  [31:0] in_2,
  input  [3:0] in_3,
  output [31:0] Output,
  output Output_2,
  output Output_3
);

  wire [30:0] Remainder;
  wire [31:0] Add, And, Div, Divu, Mult, Mulu, Nor, Or, Slt, Sltu, Sub, Xor;

  Add add_1 (.A(in_1), .B(in_2), .Result(Add));
  Sub sub_1 (.A(in_1), .B(in_2), .Result(Sub));
  Mult A_BCS (.in_1(in_1), .in_2(in_2), .Output(Mult));
  Multiplier #(.width(32)) multiplier_1 (.a(in_1), .b(in_2), .out(Mulu));  // open: cin, cout
  Div A_B_CS (.in_1(in_1), .in_2(in_2), .Output(Div), .Output_2(Remainder));
  Divider #(.width(32)) divider_1 (.a(in_1), .b(in_2), .out(Divu));  // open: upper, rem
  assign And = in_1 & in_2;  // AND_Gate and_1, 32 bits wide
  assign Or = in_1 | in_2;  // OR_Gate or_1, 32 bits wide
  assign Nor = ~(in_1 | in_2);  // NOR_Gate nor_1, 32 bits wide
  assign Xor = in_1 ^ in_2;  // XOR_Gate xor_1, 32 bits wide
  Slt slt_1 (.A(in_1), .B(in_2), .Output(Slt));
  Sltu sltu_1 (.in_1(in_1), .in_2(in_2), .Output(Sltu));
  Multiplexer #(.select(4), .width(32)) multiplexer_1 (
    .in0(Add), .in1(Sub), .in2(Mult), .in3(Mulu), .in4(Div), .in5(Divu), .in6(And), .in7(Or), .in8(Nor),
    .in9(Xor), .in10(Slt), .in11(Sltu), .out(Output), .sel(in_3));  // open: in12, in13, in14, in15, en
  Comparator #(.width(32)) comparator_1 (.a(Output), .b({32{1'b0}}), .eq(Output_2), .lt(Output_3));  // open: gt

  // Other names for the same wires on the sheet: A[31:0] = in_1; B[31:0] = in_2; OP[3:0] = in_3
endmodule

module Add (
  input  [31:0] A,
  input  [31:0] B,
  output [31:0] Result
);

  wire idx, OS, SIGN;
  wire [30:0] adder_1_out, multiplexer_2_out, subtractor_1_out, tunnel, tunnel_t;

  Multiplexer multiplexer_1 (.in0(A[31]), .in1(B[31]), .out(SIGN), .sel(idx));  // open: en
  xor xor_1 (OS, A[31], B[31]);
  circuit part_1 (.A(A[30:0]), .B(B[30:0]), .idx(idx), .out_4(tunnel_t), .out_5(tunnel));
  Adder #(.width(31)) adder_1 (.a(tunnel_t), .b(tunnel), .out(adder_1_out));  // open: cin, cout
  Subtractor #(.width(31)) subtractor_1 (.a(tunnel_t), .b(tunnel), .out(subtractor_1_out));  // open: bin, bout
  Multiplexer #(.width(31)) multiplexer_2 (
    .in0(adder_1_out), .in1(subtractor_1_out), .out(multiplexer_2_out), .sel(OS));  // open: en
  assign Result = {{1{SIGN}}, multiplexer_2_out};  // Bit_Extender bit_extender_1

  // Other names for the same wires on the sheet: MA[30:0] = A[30:0]; SA = A[31]; MB[30:0] = B[30:0]; SB = B[31]
endmodule

module Sub (
  input  [31:0] A,
  input  [31:0] B,
  output [31:0] Result
);

  wire [31:0] minus_B;

  Add add_1 (.A(A), .B(minus_B), .Result(Result));
  Mult mult_1 (.in_1(B), .in_2(32'h80000001), .Output(minus_B));

  // Other names for the same wires on the sheet: A_B_star[31:0] = Result
endmodule

module Mult (
  input  [31:0] in_1,
  input  [31:0] in_2,
  output [31:0] Output
);

  wire xor_1_out;
  wire [30:0] multiplier_1_out;

  xor xor_1 (xor_1_out, in_1[31], in_2[31]);
  Multiplier #(.width(31)) multiplier_1 (.a(in_1[30:0]), .b(in_2[30:0]), .out(multiplier_1_out));  // open: cin, cout
  assign Output = {{1{xor_1_out}}, multiplier_1_out};  // Bit_Extender bit_extender_1

  // Other names for the same wires on the sheet: A[31:0] = in_1; A_B_SIGN[31:0] = Output; B[31:0] = in_2
endmodule

module Div (
  input  [31:0] in_1,
  input  [31:0] in_2,
  output [31:0] Output,
  output [30:0] Output_2
);

  wire xor_1_out;
  wire [30:0] divider_1_out;

  xor xor_1 (xor_1_out, in_1[31], in_2[31]);
  Divider #(.width(31)) divider_1 (.a(in_1[30:0]), .b(in_2[30:0]), .out(divider_1_out), .rem(Output_2));  // open: upper
  assign Output = {{1{xor_1_out}}, divider_1_out};  // Bit_Extender bit_extender_1

  // Other names for the same wires on the sheet: A[31:0] = in_1; A_B_SIGN[31:0] = Output; B[31:0] = in_2;
  //   Remainder[30:0] = Output_2
endmodule

module Slt (
  input  [31:0] A,
  input  [31:0] B,
  output [31:0] Output
);

  wire comparator_1_lt, IM, multiplexer_2_out, not_1_out, SM;

  Multiplexer multiplexer_1 (.in0(A[31]), .in1(B[31]), .out(SM), .sel(IM));  // open: en
  Comparator #(.width(31), .mode("unsigned")) comparator_1 (
    .a(A[30:0]), .b(B[30:0]), .lt(comparator_1_lt));  // open: gt, eq
  circuit part_1 (.A(A[30:0]), .B(B[30:0]), .idx(IM));  // open: out_4, out_5
  not not_1 (not_1_out, comparator_1_lt);
  Multiplexer multiplexer_2 (.in0(comparator_1_lt), .in1(not_1_out), .out(multiplexer_2_out), .sel(SM));  // open: en
  assign Output = {{31{1'b0}}, multiplexer_2_out};  // Bit_Extender bit_extender_1

  // Other names for the same wires on the sheet: MA[30:0] = A[30:0]; SA = A[31]; MB[30:0] = B[30:0]; SB = B[31]
endmodule

module Sltu (
  input  [31:0] in_1,
  input  [31:0] in_2,
  output [31:0] Output
);

  wire comparator_1_lt;

  Comparator #(.width(32)) comparator_1 (.a(in_1), .b(in_2), .lt(comparator_1_lt));  // open: gt, eq
  assign Output = {{31{1'b0}}, comparator_1_lt};  // Bit_Extender bit_extender_1

  // Other names for the same wires on the sheet: A[31:0] = in_1; A_B[31:0] = Output; B[31:0] = in_2
endmodule

module circuit (
  input  [30:0] A,
  input  [30:0] B,
  output idx,
  output [30:0] out_4,
  output [30:0] out_5
);

  Comparator #(.width(31), .mode("unsigned")) comparator_1 (.a(A), .b(B), .lt(idx));  // open: gt, eq
  Multiplexer #(.width(31)) multiplexer_1 (.in0(A), .in1(B), .out(out_4), .sel(idx));  // open: en
  Multiplexer #(.width(31)) multiplexer_2 (.in0(B), .in1(A), .out(out_5), .sel(idx));  // open: en
endmodule

module RegisterFile (
  input  [4:0] in_1,
  input  [4:0] in_2,
  input  [4:0] in_3,
  input  [31:0] in_4,
  input  in_5,
  input  in_6,
  input  in_7,
  output [31:0] Output,
  output [31:0] Output_2
);

  wire L1, L2, L3, L4, L5, L6, L7, L8, L9, L10, L11, L12, L13, L14, L15, L16, L17, L18, L19, L20, L21, L22,
       L23, L24, L25, L26, L27, L28, L29, L30, L31;
  wire [31:0] R1, R2, R3, R4, R5, R6, R7, R8, R9, R10, R11, R12, R13, R14, R15, R16, R17, R18, R19, R20, R21,
       R22, R23, R24, R25, R26, R27, R28, R29, R30, R31;

  Demultiplexer #(.select(5)) demultiplexer_1 (
    .out1(L1), .out2(L2), .out3(L3), .out4(L4), .out5(L5), .out6(L6), .out7(L7), .out8(L8), .out9(L9),
    .out10(L10), .out11(L11), .out12(L12), .out13(L13), .out14(L14), .out15(L15), .out16(L16), .out17(L17),
    .out18(L18), .out19(L19), .out20(L20), .out21(L21), .out22(L22), .out23(L23), .out24(L24), .out25(L25),
    .out26(L26), .out27(L27), .out28(L28), .out29(L29), .out30(L30), .out31(L31), .in(in_5), .sel(in_3));  // open: out0, en
  Register #(.width(32)) u_R1 (.D(in_4), .en(L1), .Q(R1), .clk(in_6), .clr(in_7));
  Register #(.width(32)) u_R2 (.D(in_4), .en(L2), .Q(R2), .clk(in_6), .clr(in_7));
  Register #(.width(32)) u_R3 (.D(in_4), .en(L3), .Q(R3), .clk(in_6), .clr(in_7));
  Register #(.width(32)) u_R4 (.D(in_4), .en(L4), .Q(R4), .clk(in_6), .clr(in_7));
  Register #(.width(32)) u_R5 (.D(in_4), .en(L5), .Q(R5), .clk(in_6), .clr(in_7));
  Register #(.width(32)) u_R6 (.D(in_4), .en(L6), .Q(R6), .clk(in_6), .clr(in_7));
  Register #(.width(32)) u_R7 (.D(in_4), .en(L7), .Q(R7), .clk(in_6), .clr(in_7));
  Register #(.width(32)) u_R8 (.D(in_4), .en(L8), .Q(R8), .clk(in_6), .clr(in_7));
  Register #(.width(32)) u_R9 (.D(in_4), .en(L9), .Q(R9), .clk(in_6), .clr(in_7));
  Register #(.width(32)) u_R10 (.D(in_4), .en(L10), .Q(R10), .clk(in_6), .clr(in_7));
  Register #(.width(32)) u_R11 (.D(in_4), .en(L11), .Q(R11), .clk(in_6), .clr(in_7));
  Register #(.width(32)) u_R12 (.D(in_4), .en(L12), .Q(R12), .clk(in_6), .clr(in_7));
  Register #(.width(32)) u_R13 (.D(in_4), .en(L13), .Q(R13), .clk(in_6), .clr(in_7));
  Register #(.width(32)) u_R14 (.D(in_4), .en(L14), .Q(R14), .clk(in_6), .clr(in_7));
  Register #(.width(32)) u_R15 (.D(in_4), .en(L15), .Q(R15), .clk(in_6), .clr(in_7));
  Register #(.width(32)) u_R16 (.D(in_4), .en(L16), .Q(R16), .clk(in_6), .clr(in_7));
  Register #(.width(32)) u_R17 (.D(in_4), .en(L17), .Q(R17), .clk(in_6), .clr(in_7));
  Register #(.width(32)) u_R18 (.D(in_4), .en(L18), .Q(R18), .clk(in_6), .clr(in_7));
  Register #(.width(32)) u_R19 (.D(in_4), .en(L19), .Q(R19), .clk(in_6), .clr(in_7));
  Register #(.width(32)) u_R20 (.D(in_4), .en(L20), .Q(R20), .clk(in_6), .clr(in_7));
  Register #(.width(32)) u_R21 (.D(in_4), .en(L21), .Q(R21), .clk(in_6), .clr(in_7));
  Register #(.width(32)) u_R22 (.D(in_4), .en(L22), .Q(R22), .clk(in_6), .clr(in_7));
  Register #(.width(32)) u_R23 (.D(in_4), .en(L23), .Q(R23), .clk(in_6), .clr(in_7));
  Register #(.width(32)) u_R24 (.D(in_4), .en(L24), .Q(R24), .clk(in_6), .clr(in_7));
  Register #(.width(32)) u_R25 (.D(in_4), .en(L25), .Q(R25), .clk(in_6), .clr(in_7));
  Register #(.width(32)) u_R26 (.D(in_4), .en(L26), .Q(R26), .clk(in_6), .clr(in_7));
  Register #(.width(32)) u_R27 (.D(in_4), .en(L27), .Q(R27), .clk(in_6), .clr(in_7));
  Register #(.width(32)) u_R28 (.D(in_4), .en(L28), .Q(R28), .clk(in_6), .clr(in_7));
  Register #(.width(32)) u_R29 (.D(in_4), .en(L29), .Q(R29), .clk(in_6), .clr(in_7));
  Register #(.width(32)) u_R30 (.D(in_4), .en(L30), .Q(R30), .clk(in_6), .clr(in_7));
  Register #(.width(32)) u_R31 (.D(in_4), .en(L31), .Q(R31), .clk(in_6), .clr(in_7));
  Multiplexer #(.select(5), .width(32)) multiplexer_1 (
    .in0({32{1'b0}}), .in1(R1), .in2(R2), .in3(R3), .in4(R4), .in5(R5), .in6(R6), .in7(R7), .in8(R8),
    .in9(R9), .in10(R10), .in11(R11), .in12(R12), .in13(R13), .in14(R14), .in15(R15), .in16(R16), .in17(R17),
    .in18(R18), .in19(R19), .in20(R20), .in21(R21), .in22(R22), .in23(R23), .in24(R24), .in25(R25),
    .in26(R26), .in27(R27), .in28(R28), .in29(R29), .in30(R30), .in31(R31), .out(Output), .sel(in_1));  // open: en
  Multiplexer #(.select(5), .width(32)) multiplexer_2 (
    .in0({32{1'b0}}), .in1(R1), .in2(R2), .in3(R3), .in4(R4), .in5(R5), .in6(R6), .in7(R7), .in8(R8),
    .in9(R9), .in10(R10), .in11(R11), .in12(R12), .in13(R13), .in14(R14), .in15(R15), .in16(R16), .in17(R17),
    .in18(R18), .in19(R19), .in20(R20), .in21(R21), .in22(R22), .in23(R23), .in24(R24), .in25(R25),
    .in26(R26), .in27(R27), .in28(R28), .in29(R29), .in30(R30), .in31(R31), .out(Output_2), .sel(in_2));  // open: en

  // Other names for the same wires on the sheet: CLOCK = in_6; DA[31:0] = Output; DB[31:0] = Output_2; RESET = in_7;
  //   RR1[4:0] = in_1; RR2[4:0] = in_2; RW = in_5; WD[31:0] = in_4; WR[4:0] = in_3
endmodule

module Spliter (
  input  [31:0] in_1,
  output [5:0] out_2,
  output [4:0] out_3,
  output [4:0] out_4,
  output [4:0] out_5,
  output [5:0] out_6,
  output [31:0] Unsigned,
  output [31:0] Signed,
  output [25:0] out_9
);

  assign Unsigned = {{16{1'b0}}, in_1[15:0]};  // Bit_Extender bit_extender_1
  assign Signed = {{16{in_1[15]}}, in_1[15:0]};  // Bit_Extender bit_extender_2

  assign out_2 = in_1[31:26];
  assign out_3 = in_1[25:21];
  assign out_4 = in_1[20:16];
  assign out_5 = in_1[15:11];
  assign out_6 = in_1[5:0];
  assign out_9 = in_1[25:0];

  // Other names for the same wires on the sheet: Const[15:0] = in_1[15:0]; FuncCode[5:0] = in_1[5:0];
  //   Instruction[31:0] = in_1; Target[25:0] = in_1[25:0]; RD[4:0] = in_1[15:11]; RT[4:0] = in_1[20:16];
  //   RS[4:0] = in_1[25:21]; OP_Code[5:0] = in_1[31:26]
endmodule
