// Logisim project Test.circ as structural Verilog
module S_MIPS_Board (
  input  DESHABILITAR_DISPATCHER,
  output halt
);

  wire CLK, CS, d_ff_1_q, d_ff_1_qn, LCLR, LoadRAM, LoadRAMOn, multiplexer_5_out, R_R_W, R_W, ram_1_p2,
       ram_1_p4, ram_1_p6, ram_1_p7, ram_1_p11, ram_1_p12, ram_1_p13, ram_1_p14, ram_1_p15, RCS, Reset_out,
       RST, TTY_EN, undriven, undriven_2, undriven_3, undriven_4;
  wire [2:0] KDB;
  wire [3:0] LMask, LW, Mask, ram_1_p10, RMask;
  wire [6:0] KDB_DATA, TTY_DATA;
  wire [15:0] Addr, LAddr, RAddr;
  wire [31:0] I0, I1, I2, I3, LData, RI1, RI2, RI3, s_mips_1_p9;

  TTY #(.rows(25), .cols(80)) tty_1 (.data(TTY_DATA), .clk(CLK), .we(TTY_EN), .clr(RST));
  not not_1 (LoadRAMOn, undriven);
  RAM_Dispatcher ram_dispatcher_1 (
    .WriteTime_2(ram_1_p10), .Clock_3(CLK), .Data(LData), .Address(LAddr), .Mask_2(LMask), .Write(LW[0]),
    .CLR(LCLR));
  RAM_Dispatcher ram_dispatcher_2 (
    .WriteTime_2(ram_1_p10), .Clock_3(CLK), .Data(LData), .Address(LAddr), .Mask_2(LMask), .Write(LW[0]),
    .CLR(LCLR));
  Keyboard #(.buflen(64)) keyboard_1 (.clk(CLK), .re(KDB[0]), .avail(KDB[2]), .data(KDB_DATA));  // open: clr
  // RAM ram_1: pin names not known; wires that end beside it: RAddr, ram_1_p2, RI1, ram_1_p4, R_W, ram_1_p6, ram_1_p7, R_R_W, RCS, ram_1_p10, ram_1_p11, ram_1_p12, ram_1_p13, ram_1_p14, ram_1_p15
  // RAM ram_2: pin names not known; wires that end beside it: RAddr, ram_1_p2, RI1, ram_1_p4, R_W, ram_1_p6, ram_1_p7, R_R_W, RCS, ram_1_p10, ram_1_p11, ram_1_p12, ram_1_p13, ram_1_p14, ram_1_p15
  Button button_1 (.out(ram_1_p11));
  D_Flip_Flop d_ff_1 (
    .clk(CLK), .D(1'b1), .Q(d_ff_1_q), .Qn(d_ff_1_qn), .preset(undriven_2), .en(undriven_3), .reset(Reset_out));
  D_Flip_Flop d_ff_2 (
    .clk(CLK), .D(1'b1), .Q(d_ff_1_q), .Qn(d_ff_1_qn), .preset(undriven_2), .en(undriven_3), .reset(Reset_out));
  D_Flip_Flop d_ff_3 (
    .clk(CLK), .D(1'b1), .Q(d_ff_1_q), .Qn(d_ff_1_qn), .preset(undriven_2), .en(undriven_3), .reset(Reset_out));
  Button Reset (.out(Reset_out));
  // S_MIPS s_mips_1: pin names not known; wires that end beside it: Addr, ram_1_p12, ram_1_p13, ram_1_p14, ram_1_p15, I0, I1, I2, s_mips_1_p9, Mask, ram_1_p7, RST, ram_1_p10, CLK, R_W, CS, halt, TTY_EN, TTY_DATA, KDB[0], KDB[1], KDB[2], KDB_DATA
  D_Flip_Flop d_ff_4 (.clk(CLK), .D(d_ff_1_q), .Qn(LCLR), .reset(Reset_out));  // open: Q, preset, en
  or or_1 (RST, LCLR, LoadRAM);
  Clock clock_1 (.out(CLK));
  Clock clock_2 (.out(CLK));
  Multiplexer #(.width(32), .enable("false")) multiplexer_1 (.in0(I0), .in1(RI1), .out(I2), .sel(LoadRAM));
  Multiplexer #(.width(32)) u_RI1 (.in0(I1), .in1(LData), .out(RI1), .sel(LoadRAM));  // open: en
  Multiplexer #(.width(32), .enable("false")) multiplexer_2 (.in0(I2), .in1(LData), .out(RI2), .sel(LoadRAM));
  Multiplexer #(.width(32), .enable("false")) multiplexer_3 (.in0(I3), .in1(LData), .out(RI3), .sel(LoadRAM));
  and and_1 (LoadRAM, ~DESHABILITAR_DISPATCHER, LoadRAMOn);  // AND_Gate
  and and_2 (LoadRAM, ~DESHABILITAR_DISPATCHER, LoadRAMOn);  // AND_Gate
  and and_3 (LoadRAM, ~DESHABILITAR_DISPATCHER, LoadRAMOn);  // AND_Gate
  Multiplexer #(.width(4), .enable("false")) multiplexer_4 (.in0(LW), .in1(LMask), .out(RMask), .sel(LoadRAM));
  Multiplexer #(.enable("false")) multiplexer_5 (.in0(CS), .in1(LW[0]), .out(multiplexer_5_out), .sel(LoadRAM));
  Multiplexer #(.enable("false")) multiplexer_6 (.in0(R_W), .in1(undriven_4), .out(R_R_W), .sel(LoadRAM));
  // Pins of 1 and 4 bits meet at LW

  // Notes on the sheet:
  //   NO MODIFICAR
  //   Keyboard
endmodule

module RAM (
  input  [15:0] Address,
  input  [31:0] Data_In_1,
  input  [31:0] Data_In_2,
  input  [31:0] Data_In_2_2,
  input  [31:0] Data_In_3,
  input  [3:0] Mask,
  input  [3:0] Mask_2,
  input  nRead_Write,
  input  Chip_Select,
  input  Reset,
  output [31:0] Data_Out_0,
  output [31:0] Data_Out_1,
  output [3:0] Read_Time,
  output [3:0] Write_Time
);

  wire and_1_out, and_2_out, and_4_out, and_5_out, and_6_out, and_7_out, and_8_out, and_9_out, and_10_out,
       Changed, comparator_2_eq, comparator_3_eq, comparator_4_eq, comparator_5_eq, comparator_5_gt,
       comparator_5_lt, comparator_7_eq, Count, demultiplexer_1_out0, demultiplexer_2_out1,
       demultiplexer_3_out0, Idle, Idle_q, Idle_qn, Load, Load0, Load1, nand_1_out, or_1_out, or_2_out,
       or_3_out, or_4_out, or_5_out, or_6_out, or_7_out, or_8_out, or_9_out, or_11_out, Proc_q, undriven,
       undriven_2, undriven_5, undriven_6, undriven_7, undriven_10, undriven_11, Update_Mem, Zero_Time;
  wire [3:0] counter_1_q, multiplexer_1_out, subtractor_1_out, undriven_4;
  wire [15:0] CLK, undriven_8;
  wire [15:1] M3, RW;
  wire [20:17] undriven_3;
  wire [31:0] Data_In_0, Data_Out_2, Data_Out_3, register_1_q, register_2_q, register_3_q, register_4_q,
       register_5_q, undriven_9;

  // Probe on Read_Time
  // Probe on 4'b0010
  Multiplexer #(.width(4), .enable("false")) multiplexer_1 (
    .in0(Read_Time), .in1(4'b0010), .out(multiplexer_1_out), .sel(nRead_Write));
  or or_1 (or_1_out, demultiplexer_1_out0, demultiplexer_2_out1);
  or or_2 (or_2_out, ~Chip_Select, Reset);  // OR_Gate
  Subtractor #(.width(4)) subtractor_1 (.a(multiplexer_1_out), .b(4'b0010), .out(subtractor_1_out));  // open: bin, bout
  D_Flip_Flop u_Idle (
    .clk(CLK[0]), .D(or_1_out), .Q(Idle_q), .Qn(Idle_qn), .preset(or_2_out), .en(undriven), .reset(undriven_2));
  Demultiplexer #(.enable("false")) demultiplexer_1 (
    .out0(demultiplexer_1_out0), .out1(Load0), .in(Idle_q), .sel(Changed));
  D_Flip_Flop Idle_2 (
    .clk(CLK[0]), .D(or_1_out), .Q(Idle_q), .Qn(Idle_qn), .preset(or_2_out), .en(undriven), .reset(undriven_2));
  // Probe on counter_1_q
  Counter #(.width(4), .max('hf)) counter_1 (
    .load(Load), .D(subtractor_1_out), .count(Count), .Q(counter_1_q), .clk(CLK[0]), .clr(or_3_out));  // open: carry
  or or_3 (or_3_out, ~Chip_Select, Reset);  // OR_Gate
  Comparator #(.width(4), .mode("unsigned")) comparator_1 (
    .a(undriven_4), .b(counter_1_q), .eq(Zero_Time));  // open: gt, lt
  or or_4 (or_4_out, Count, Load0, Load1);
  Register #(.width(32)) register_1 (.D(Data_In_0), .en(Chip_Select), .Q(register_1_q), .clk(CLK[0]), .clr(or_5_out));
  or or_5 (or_5_out, ~Chip_Select, Reset);  // OR_Gate
  Register #(.width(32)) register_2 (.D(Data_In_1), .en(Chip_Select), .Q(register_2_q), .clk(CLK[0]), .clr(or_6_out));
  or or_6 (or_6_out, ~Chip_Select, Reset);  // OR_Gate
  Register #(.width(32)) register_3 (.D(Data_In_2), .en(Chip_Select), .Q(register_3_q), .clk(CLK[0]), .clr(or_7_out));
  or or_7 (or_7_out, ~Chip_Select, Reset);  // OR_Gate
  Register #(.width(32)) register_4 (.D(Data_In_0), .en(Chip_Select), .Q(register_4_q), .clk(CLK[0]), .clr(or_8_out));
  or or_8 (or_8_out, ~Chip_Select, Reset);  // OR_Gate
  Register #(.width(32)) register_5 (
    .D({{11{1'b1}}, undriven_3[20], Mask[3:2], undriven_3[17], Mask[0], M3, Mask[3]}), .en(Chip_Select),
    .Q(register_5_q), .clk(CLK[0]), .clr(or_9_out));
  Register #(.width(32)) register_6 (
    .D({{11{1'b1}}, undriven_3[20], Mask[3:2], undriven_3[17], Mask[0], M3, Mask[3]}), .en(Chip_Select),
    .Q(register_5_q), .clk(CLK[0]), .clr(or_9_out));
  or or_9 (or_9_out, ~Chip_Select, Reset);  // OR_Gate
  or or_10 (or_9_out, ~Chip_Select, Reset);  // OR_Gate
  D_Flip_Flop Proc (.clk(CLK[0]), .D(or_4_out), .Q(Proc_q), .reset(or_11_out));  // open: Qn, preset, en
  or or_11 (or_11_out, ~Chip_Select, Reset);  // OR_Gate
  Demultiplexer #(.enable("false")) demultiplexer_2 (
    .out0(Count), .out1(demultiplexer_2_out1), .in(demultiplexer_3_out0));  // open: sel
  Demultiplexer #(.enable("false")) demultiplexer_3 (
    .out0(demultiplexer_3_out0), .out1(Load1), .in(Proc_q), .sel(Changed));
  Clock clock_1 (.out(CLK[0]));
  Comparator #(.width(32)) comparator_2 (.a(register_1_q), .b(Data_In_0), .eq(comparator_2_eq));  // open: gt, lt
  Comparator #(.width(32)) comparator_3 (.a(register_2_q), .b(Data_In_1), .eq(comparator_3_eq));  // open: gt, lt
  Comparator #(.width(32)) comparator_4 (.a(register_3_q), .b(Data_In_2), .eq(comparator_4_eq));  // open: gt, lt
  Comparator #(.width(32)) comparator_5 (
    .a(register_4_q), .b(Data_In_0), .gt(comparator_5_gt), .eq(comparator_5_eq), .lt(comparator_5_lt));
  Comparator #(.width(32)) comparator_6 (
    .a(register_4_q), .b(Data_In_0), .gt(comparator_5_gt), .eq(comparator_5_eq), .lt(comparator_5_lt));
  Comparator #(.width(32)) comparator_7 (
    .a(register_5_q), .b({{11{1'b1}}, undriven_3[20], Mask[3:2], undriven_3[17], Mask[0], M3, Mask[3]}),
    .eq(comparator_7_eq));  // open: gt, lt
  nand nand_1 (nand_1_out, comparator_7_eq, comparator_2_eq, comparator_3_eq, comparator_4_eq, comparator_5_eq);
  nand nand_2 (nand_1_out, comparator_7_eq, comparator_2_eq, comparator_3_eq, comparator_4_eq, comparator_5_eq);
  and and_1 (and_1_out, nand_1_out, Chip_Select);
  or or_12 (Load, undriven_5, Mask[3], Load0);
  and and_2 (and_2_out, Mask[0], Update_Mem, undriven_6);
  and and_3 (and_2_out, Mask[0], Update_Mem, undriven_6);
  and and_4 (and_4_out, Mask[1], Update_Mem, nRead_Write);
  and and_5 (and_5_out, Mask[2], Update_Mem, undriven_7);
  and and_6 (and_6_out, Mask[3], Update_Mem, nRead_Write);
  RAM_part #(.addrWidth(16), .dataWidth(32), .bus("separate")) ram_1 (
    .addr({RW, nRead_Write}), .din(Data_In_0), .data(Data_Out_0), .str(and_2_out), .sel(Chip_Select),
    .clk(CLK[0]), .ld(and_7_out), .clr(CLK[0]));
  RAM_part #(.addrWidth(16), .dataWidth(32), .bus("separate")) ram_2 (
    .addr({RW, nRead_Write}), .din(Data_In_0), .data(Data_Out_0), .str(and_2_out), .sel(Chip_Select),
    .clk(CLK[0]), .ld(and_7_out), .clr(CLK[0]));
  and and_7 (and_7_out, ~nRead_Write, Idle);  // AND_Gate
  RAM_part #(.addrWidth(16), .dataWidth(32), .bus("separate")) ram_3 (
    .addr(CLK), .din(Data_In_1), .data(Data_Out_1), .str(and_4_out), .sel(Chip_Select), .clk(CLK[0]),
    .ld(and_8_out), .clr(Reset));
  and and_8 (and_8_out, ~undriven_11, Idle);  // AND_Gate
  RAM_part #(.addrWidth(16), .dataWidth(32), .bus("separate")) ram_4 (
    .addr(Address), .din(Data_In_2), .data(Data_Out_2), .str(and_5_out), .sel(Chip_Select), .clk(CLK[0]),
    .ld(and_9_out), .clr(Reset));
  RAM_part #(.addrWidth(16), .dataWidth(32), .bus("separate")) ram_5 (
    .addr(Address), .din(Data_In_2), .data(Data_Out_2), .str(and_5_out), .sel(Chip_Select), .clk(CLK[0]),
    .ld(and_9_out), .clr(Reset));
  and and_9 (and_9_out, ~nRead_Write, Idle);  // AND_Gate
  RAM_part #(.addrWidth(16), .dataWidth(32), .bus("separate")) ram_6 (
    .addr(undriven_8), .din(undriven_9), .data(Data_Out_3), .str(and_6_out), .sel(undriven_10), .clk(CLK[0]),
    .ld(and_10_out), .clr(Reset));
  and and_10 (and_10_out, ~nRead_Write, Idle);  // AND_Gate
  // Pins of 1 and 16 bits meet at CLK
  // Pins of 1 and 16 bits meet at {RW, nRead_Write}
  // Pins of 1 and 16 bits meet at {M3, Mask[3]}

  assign Data_In_2_2 = Data_In_2;
  assign Mask_2 = Mask;
  assign Write_Time = 4'b0010;

  // Other names for the same wires on the sheet: M0 = Mask[0]; M2 = Mask[2]; M3[0] = Mask[3]; CLR = Reset;
  //   CS = Chip_Select; Data_In_3_t[31:0] = Data_In_0; Load2 = Count; M1 = Mask[1]; RT[3:0] = Read_Time;
  //   RW[0] = nRead_Write

  // Notes on the sheet:
  //   NO MODIFICAR
  //   excepto quizás los valores RT y WT
  //   BANK0
  //   BANK1
  //   BANK2
endmodule

module S_MIPS (
  input  Kbd_Available,
  input  [6:0] Kbd_ASCII_Data,
  input  [31:0] RAM_Out_0,
  input  [31:0] RAM_Out_1,
  input  Reset,
  input  [31:0] RAM_Out_2,
  input  Clock,
  input  [31:0] RAM_Out_3,
  input  [3:0] Read_Time,
  input  [3:0] Write_Time,
  input  [3:0] Write_Time_2,
  output Kbd_Enable,
  output Kbd_Clear,
  output [6:0] TTY_Enable,
  output [6:0] TTY_ASCII_Data,
  output Stop,
  output [31:0] RAM_In_0,
  output [31:0] RAM_In_2,
  output [31:0] RAM_In_2_2,
  output [31:0] RAM_In_3,
  output [3:0] Mask,
  output nRead_Write,
  output Stop_2
);

  // Pins of 1 and 7 bits meet at TTY_Enable

  assign RAM_In_2_2 = RAM_In_2;
  assign Write_Time_2 = Write_Time;

  // Other names for the same wires on the sheet: CLK = Clock; CLR = Reset; CS = Stop_2; KBD_AVAIL = Kbd_Available;
  //   KBD_CLR = Kbd_Clear; KBD_DATA[6:0] = Kbd_ASCII_Data; RAM_INPUT_0[31:0] = RAM_In_0; RAM_INPUT_2[31:0] = RAM_In_2;
  //   RAM_INPUT_3[31:0] = RAM_In_3; RAM_MASK[3:0] = Mask; RAM_OUTPUT_1[31:0] = RAM_Out_1;
  //   RAM_OUTPUT_2[31:0] = RAM_Out_2; RW = nRead_Write; TTY_DATA[6:0] = TTY_ASCII_Data

  // Notes on the sheet:
  //   RAM ADDRESS
  //   DATA FROM RAM
  //   DATA TO RAM
  //   DATA WRITE MASK
  //   RAM TIMING
  //   RAM CONTROL
  //   KEYBOARD
  //   TTY
  //   SEQUENCING
endmodule

module RAM_Dispatcher (
  input  [3:0] WriteTime,
  input  [3:0] WriteTime_2,
  input  Clock,
  input  Clock_2,
  input  Clock_3,
  input  CLR,
  output [31:0] Data,
  output [3:0] Mask,
  output [15:0] Address,
  output [3:0] Mask_2,
  output Write
);

  wire comparator_1_gt, comparator_1_lt, CurrentAddress_carry, demultiplexer_3_out1, End, Finished, IDLE_q,
       IDLE_qn, IncAddr, Load, or_1_out, or_2_out, undriven, undriven_2, undriven_4, undriven_5, undriven_6,
       undriven_7, undriven_8, undriven_9, undriven_10, While_q, WriteEnd;
  wire [3:0] counter_1_q;
  wire [31:0] CurrentAddress_q, undriven_3;

  Counter #(.width(32), .max('hffffffff)) CurrentAddress (
    .load(undriven_2), .D(undriven_3), .count(undriven),
    .Q({CurrentAddress_q[31:18], Address, CurrentAddress_q[1:0]}), .carry(CurrentAddress_carry), .clk(Clock),
    .clr(CLR));
  Counter #(.width(32), .max('hffffffff)) CurrentAddress_2 (
    .load(undriven_2), .D(undriven_3), .count(undriven),
    .Q({CurrentAddress_q[31:18], Address, CurrentAddress_q[1:0]}), .carry(CurrentAddress_carry), .clk(Clock),
    .clr(CLR));
  or or_1 (or_1_out, IncAddr, undriven_4, Finished);
  D_Flip_Flop IDLE (
    .clk(Clock), .D(or_1_out), .Q(IDLE_q), .Qn(IDLE_qn), .preset(CLR), .en(undriven_5), .reset(undriven_6));
  D_Flip_Flop IDLE_2 (
    .clk(Clock), .D(or_1_out), .Q(IDLE_q), .Qn(IDLE_qn), .preset(CLR), .en(undriven_5), .reset(undriven_6));
  Demultiplexer #(.enable("false")) demultiplexer_1 (.out0(Load), .out1(Finished), .in(IDLE_q), .sel(End));
  Demultiplexer #(.enable("false")) demultiplexer_2 (.out0(Load), .out1(Finished), .in(IDLE_q), .sel(End));
  D_Flip_Flop While (.clk(Clock), .D(or_2_out), .Q(While_q), .reset(CLR));  // open: Qn, preset, en
  or or_2 (or_2_out, Write, Load);
  or or_3 (or_2_out, Write, Load);
  or or_4 (or_2_out, Write, Load);
  RAM_part #(.addrWidth(18), .dataWidth(32)) ram_1 (
    .addr({Address, CurrentAddress_q[1:0]}), .data(Data), .sel(undriven_7), .clk(Clock), .ld(undriven_8),
    .clr(undriven_9));
  RAM_part #(.addrWidth(18), .dataWidth(32)) ram_2 (
    .addr({Address, CurrentAddress_q[1:0]}), .data(Data), .sel(undriven_7), .clk(Clock), .ld(undriven_8),
    .clr(undriven_9));
  Demultiplexer #(.enable("false")) demultiplexer_3 (
    .out0(Write), .out1(demultiplexer_3_out1), .in(While_q), .sel(WriteEnd));
  Decoder #(.select(2)) decoder_1 (.sel(CurrentAddress_q[1:0]));  // open: out0, out1, out2, out3, en
  Counter #(.width(4), .max('hf)) counter_1 (
    .load(Load), .D(WriteTime), .count(Write), .Q(counter_1_q), .clk(undriven_10));  // open: carry, clr
  Comparator #(.width(32)) comparator_1 (
    .a(Data), .b({32{1'b1}}), .gt(comparator_1_gt), .eq(End), .lt(comparator_1_lt));
  Comparator #(.width(32)) comparator_2 (
    .a(Data), .b({32{1'b1}}), .gt(comparator_1_gt), .eq(End), .lt(comparator_1_lt));
  Comparator #(.width(4)) comparator_3 (.a(4'b0000), .b(counter_1_q), .eq(WriteEnd));  // open: gt, lt
  // Pins of 4 and 16 bits meet at Address

  assign Clock_2 = Clock;
  assign Clock_3 = Clock;
  assign Mask = Address[3:0];
  assign WriteTime_2 = WriteTime;

  // Other names for the same wires on the sheet: CLK = Clock; Count = Write; WT[3:0] = WriteTime
endmodule

module ALU (
  input  [31:0] in_1,
  input  [3:0] in_2,
  output [31:0] Output,
  output Output_2,
  output Output_3
);

  wire A_B_CS_p2, A_B_CS_p4, A_B_CS_p8, A_BCS_p2, A_BCS_p4, A_BCS_p5, A_BCS_p6, add_1_p1, add_1_p3, add_1_p5,
       add_1_p6, comparator_1_eq, comparator_1_lt, divider_1_p2, divider_1_p3, divider_1_p7,
       multiplexer_2_p1, multiplexer_2_p2, multiplexer_2_p3, multiplexer_2_p4, multiplexer_2_p6,
       multiplexer_2_p8, multiplier_1_p2, multiplier_1_p3, multiplier_1_p4, multiplier_1_p6, MuluLo_p2,
       sub_1_p1, sub_1_p3, sub_1_p5;
  wire [2:0] multiplexer_2_p9;
  wire [30:0] Remainder;
  wire [31:0] A, Add, And, B, Div, Divu, Mult, multiplexer_1_out, multiplexer_2_p5, Mulu, Nor, or_1_out, Slt,
       Sltu, Sub, undriven, undriven_2, undriven_3, undriven_4, undriven_5, undriven_6, undriven_7, Xor,
       xor_1_out;

  // Add add_1: pin names not known; wires that end beside it: add_1_p1, add_1_p1, add_1_p3, Add, add_1_p5, add_1_p6, add_1_p6
  // Sub sub_1: pin names not known; wires that end beside it: sub_1_p1, sub_1_p1, sub_1_p3, Sub, sub_1_p5
  // Mult A_BCS: pin names not known; wires that end beside it: sub_1_p3, A_BCS_p2, A_BCS_p2, A_BCS_p4, A_BCS_p5, A_BCS_p6, Mult
  // Multiplier #(.width(32)) multiplier_1: pin names not known; wires that end beside it: A_BCS_p4, multiplier_1_p2, multiplier_1_p3, multiplier_1_p4, Mulu, multiplier_1_p6, A_BCS_p6
  // Div A_B_CS: pin names not known; wires that end beside it: multiplier_1_p3, A_B_CS_p2, A_B_CS_p2, A_B_CS_p4, Remainder, multiplier_1_p4, Div, A_B_CS_p8
  // Divider #(.width(32)) divider_1: pin names not known; wires that end beside it: A_B_CS_p4, divider_1_p2, divider_1_p3, divider_1_p2, divider_1_p3, Divu, divider_1_p7
  assign And = A & Sub;  // AND_Gate and_1, 32 bits wide
  assign or_1_out = A | A;  // OR_Gate or_1, 32 bits wide
  assign Nor = ~(A | B);  // NOR_Gate nor_1, 32 bits wide
  assign xor_1_out = A ^ B;  // XOR_Gate xor_1, 32 bits wide
  Slt slt_1 (.A_2(B), .B(B), .Output(Slt));  // open: A, B_2
  Sltu sltu_1 (.B(A), .in_2(B), .Output(Sltu));  // open: A
  Multiplexer #(.select(3), .width(32)) multiplexer_1 (
    .in0(undriven), .in1(undriven_6), .in2(undriven_2), .in3(undriven_3), .in4(undriven_4), .in5(Xor),
    .in6(undriven_5), .in7(multiplexer_2_p5), .out(multiplexer_1_out), .sel(multiplexer_2_p9));  // open: en
  // Multiplexer #(.select(4), .width(32)) multiplexer_2: pin names not known; wires that end beside it: multiplexer_2_p1, multiplexer_2_p2, multiplexer_2_p3, multiplexer_2_p4, multiplexer_2_p5, multiplexer_2_p6, in_2, multiplexer_2_p8, multiplexer_2_p9
  Comparator #(.width(32)) comparator_1 (
    .a(multiplexer_1_out), .b(undriven_7), .eq(comparator_1_eq), .lt(comparator_1_lt));  // open: gt
  // Comparator #(.width(32)) MuluLo: pin names not known; wires that end beside it: {32{1'b0}}, MuluLo_p2

  // Other names for the same wires on the sheet: OP[3:0] = in_2
endmodule

module Add (
  input  [31:0] A,
  input  [31:0] B,
  output [31:0] Result
);

  wire OS, SIGN, subtractor_1_bout, undriven_2, undriven_3;
  wire [30:0] adder_1_out, idx, multiplexer_2_out, part_1_out_4, SA, subtractor_1_out, tunnel_t, undriven;

  Multiplexer multiplexer_1 (.in0(SA[0]), .in1(B[31]), .out(SIGN), .sel(idx[0]));  // open: en
  xor xor_1 (OS, SA[0], B[31]);
  xor xor_2 (OS, SA[0], B[31]);
  circuit part_1 (.A(undriven), .B(B[30:0]), .out_3(idx), .out_4(part_1_out_4), .out_5(SA));
  Adder #(.width(31)) adder_1 (.a(tunnel_t), .b(SA), .out(adder_1_out));  // open: cin, cout
  Subtractor #(.width(31)) subtractor_1 (
    .a(tunnel_t), .b(SA), .out(subtractor_1_out), .bin(undriven_2), .bout(subtractor_1_bout));
  Subtractor #(.width(31)) subtractor_2 (
    .a(tunnel_t), .b(SA), .out(subtractor_1_out), .bin(undriven_2), .bout(subtractor_1_bout));
  Multiplexer #(.width(31)) multiplexer_2 (
    .in0(adder_1_out), .in1(subtractor_1_out), .out(multiplexer_2_out), .sel(OS), .en(undriven_3));
  Multiplexer #(.width(31)) multiplexer_3 (
    .in0(adder_1_out), .in1(subtractor_1_out), .out(multiplexer_2_out), .sel(OS), .en(undriven_3));
  assign Result = {{1{SIGN}}, multiplexer_2_out};  // Bit_Extender bit_extender_1
  // Pins of 1 and 31 bits meet at SA
  // Pins of 1 and 31 bits meet at idx

  // Other names for the same wires on the sheet: MB[30:0] = B[30:0]; SB = B[31]; tunnel[30:0] = SA
endmodule

module Sub (
  input  [31:0] B,
  input  [31:0] A,
  output [31:0] Result,
  output [31:0] Result_2
);

  wire [31:0] B_t, minus_B, undriven;

  Add add_1 (.A(undriven), .B(minus_B), .Result(Result));
  Add add_2 (.A(undriven), .B(minus_B), .Result(Result));
  Mult mult_1 (.in_1(B_t), .in_2(32'h1), .Output(A));
  Mult mult_2 (.in_1(B_t), .in_2(32'h1), .Output(A));

  assign B = A;
  assign Result_2 = Result;

  // Other names for the same wires on the sheet: A_B_star[31:0] = Result
endmodule

module Mult (
  input  [31:0] in_1,
  input  [31:0] in_2,
  output [31:0] Output
);

  wire [30:0] multiplier_1_cout, multiplier_1_out;

  Multiplier #(.width(31)) multiplier_1 (
    .a(in_1[30:0]), .b(in_1[30:0]), .out(multiplier_1_out), .cout(multiplier_1_cout));  // open: cin
  Bit_Extender #(.in_width(31), .out_width(32), .\type ("input")) bit_extender_1 (
    .in(multiplier_1_out), .out(Output));  // open: extend

  // Other names for the same wires on the sheet: A[31:0] = in_1; Hi[31:0] = in_2; A_B_SIGN[31:0] = Output;
  //   Lo[31:0] = Output
endmodule

module Div (
  input  [31:0] in_1,
  input  [31:0] in_2,
  output [31:0] Output,
  output [30:0] Output_2
);

  wire xor_1_out;
  wire [30:0] divider_1_out, undriven;
  wire [31:0] Lo, undriven_3;
  wire [31:31] undriven_2;

  xor xor_1 (xor_1_out, undriven_2[31], undriven_3[31]);
  Divider #(.width(31)) divider_1 (.a(undriven), .b(undriven_3[30:0]), .out(divider_1_out));  // open: upper, rem
  assign Lo = {{1{xor_1_out}}, divider_1_out};  // Bit_Extender bit_extender_1

  // Other names for the same wires on the sheet: A[31:0] = in_1; A_B_SIGN[31:0] = Output; B[31:0] = in_2;
  //   Remainder[30:0] = Output_2
endmodule

module Slt (
  input  [31:0] A,
  input  [31:0] A_2,
  input  [31:0] B,
  input  [31:0] B_2,
  output [31:0] Output
);

  wire comparator_1_eq, comparator_1_gt, comparator_1_lt, multiplexer_2_out, not_1_out, SB, SM;
  wire [30:0] IM, MB, part_1_out_4, part_1_out_5;

  Multiplexer multiplexer_1 (.in0(A[31]), .in1(SB), .out(SM), .sel(IM[0]));  // open: en
  Comparator #(.width(31), .mode("unsigned")) comparator_1 (
    .a(A[30:0]), .b(MB), .gt(comparator_1_gt), .eq(comparator_1_eq), .lt(comparator_1_lt));
  Comparator #(.width(31), .mode("unsigned")) comparator_2 (
    .a(A[30:0]), .b(MB), .gt(comparator_1_gt), .eq(comparator_1_eq), .lt(comparator_1_lt));
  circuit part_1 (.A(A[30:0]), .B(MB), .out_3(IM), .out_4(part_1_out_4), .out_5(part_1_out_5));
  circuit part_2 (.A(A[30:0]), .B(MB), .out_3(IM), .out_4(part_1_out_4), .out_5(part_1_out_5));
  not not_1 (not_1_out, comparator_1_lt);
  Multiplexer multiplexer_2 (.in0(comparator_1_lt), .in1(not_1_out), .out(multiplexer_2_out), .sel(SM));  // open: en
  assign Output = {{31{1'b0}}, multiplexer_2_out};  // Bit_Extender bit_extender_1
  // Pins of 1 and 31 bits meet at IM

  assign A_2 = A;
  assign B_2 = B;

  // Other names for the same wires on the sheet: MA[30:0] = A[30:0]; SA = A[31]
endmodule

module Sltu (
  input  [31:0] B,
  input  [31:0] in_2,
  output [31:0] Output,
  output [31:0] A
);

  wire comparator_1_lt;
  wire [31:0] A_B, undriven;

  Comparator #(.width(32)) comparator_1 (.a(B), .b(undriven), .lt(comparator_1_lt));  // open: gt, eq
  assign A_B = {{31{1'b0}}, comparator_1_lt};  // Bit_Extender bit_extender_1

  assign Output = A;

  // Other names for the same wires on the sheet: A_t[31:0] = B; B_t[31:0] = in_2
endmodule

module circuit (
  input  [30:0] A,
  input  [30:0] B,
  output [30:0] out_3,
  output [30:0] out_4,
  output [30:0] out_5
);

  wire comparator_1_lt, undriven;

  Comparator #(.width(31), .mode("unsigned")) comparator_1 (.a(A), .b(B), .lt(comparator_1_lt));  // open: gt, eq
  Multiplexer #(.width(31)) multiplexer_1 (.in0(B), .in1(A), .out(out_5), .sel(comparator_1_lt), .en(undriven));
  Multiplexer #(.width(31)) multiplexer_2 (.in0(B), .in1(A), .out(out_5), .sel(comparator_1_lt), .en(undriven));

  assign out_4 = out_3;
endmodule

module RegisterFile (
  input  [4:0] in_1,
  input  [4:0] in_2,
  input  [4:0] in_3,
  input  [31:0] WD,
  input  [31:0] in_5,
  input  in_6,
  input  RW,
  input  in_8,
  input  in_9,
  output [31:0] Output,
  output [31:0] Output_2
);

  wire demultiplexer_1_p9, L1, L2, L4, L6, L7, L8, L9, L10, L11, L12, L13, L15, L16, L19, L22, L23, L24, L26,
       L27, L28, L29, L31, RESET, undriven_2, undriven_4;
  wire [31:0] HiIn, L3, L5, L14, L20, L21, L25, Lo, LoIn, R1, R2, R3, R4, R5, R6, R7, R8, R9, R10, R12, R13,
       R14, R15, R16, R16_q, R17, R18, R20, R21, R22, R23, R24, R25, R26, R27, R28, R29, R30, R31, undriven,
       undriven_3;

  // Demultiplexer #(.select(5)) demultiplexer_1: pin names not known; wires that end beside it: in_6, L10, L11, L12, L13, L14, L15, L16, demultiplexer_1_p9
  Register #(.width(32)) u_R1 (.D(in_5), .en(L1), .Q(R1), .clk(in_8), .clr(in_2[0]));
  Register #(.width(32)) u_R2 (.D(R15), .en(in_5[0]), .Q(R2), .clk(RESET), .clr(RESET));
  Register #(.width(32)) R2_2 (.D(R15), .en(in_5[0]), .Q(R2), .clk(RESET), .clr(RESET));
  Register #(.width(32)) u_R3 (.D(in_5), .en(L3[0]), .Q(R3), .clk(in_8), .clr(RESET));
  Register #(.width(32)) u_R4 (.D(in_5), .en(L4), .Q(R4), .clk(in_8), .clr(RESET));
  Register #(.width(32)) u_R5 (.D(in_5), .en(L5[0]), .Q(R5), .clk(RESET), .clr(RESET));
  Register #(.width(32)) u_R6 (.D(L21), .en(L6), .Q(R6), .clk(in_8), .clr(RESET));
  Register #(.width(32)) u_R7 (.D(undriven), .en(L7), .Q(R7), .clk(in_8), .clr(RESET));
  Register #(.width(32)) u_R8 (.D(in_5), .en(L8), .Q(R8), .clk(in_8), .clr(RESET));
  Register #(.width(32)) u_R9 (.D(in_5), .en(L9), .Q(R9), .clk(in_8), .clr(RESET));
  Register #(.width(32)) u_R10 (.D(in_5), .en(L10), .Q(R10), .clk(in_8), .clr(in_8));
  Register #(.width(32)) R11 (.D(L3), .en(L11), .Q(in_5), .clk(in_8), .clr(RESET));
  Register #(.width(32)) u_R12 (.D(in_5), .en(undriven_2), .Q(R12), .clk(in_8), .clr(in_8));
  Register #(.width(32)) u_R13 (.D(Output_2), .en(L13), .Q(R13), .clk(in_8), .clr(RESET));
  Register #(.width(32)) u_R14 (.D(in_5), .en(L14[0]), .Q(R14), .clk(in_8), .clr(in_8));
  Register #(.width(32)) u_R15 (.D(R7), .en(L15), .Q(R15), .clk(in_8), .clr(RESET));
  Register #(.width(32)) u_R16 (.D(L20), .en(L16), .Q(R16_q), .clk(RESET), .clr(RESET));
  Register #(.width(32)) u_R18 (.D(Lo), .en(L2), .Q(R18), .clk(in_8), .clr(RESET));
  Register #(.width(32)) R19 (.D(in_5), .en(L19), .Q(R1), .clk(in_8), .clr(RESET));
  Register #(.width(32)) u_R20 (.D(in_5), .en(L20[0]), .Q(R20), .clk(in_8), .clr(RESET));
  Register #(.width(32)) u_R21 (.D(undriven_3), .en(L21[0]), .Q(R21), .clk(in_8), .clr(RESET));
  Register #(.width(32)) u_R22 (.D(in_5), .en(L22), .Q(R22), .clk(in_8), .clr(RESET));
  Register #(.width(32)) R22_2 (.D(in_5), .en(L23), .Q(R23), .clk(in_8), .clr(RESET));
  Register #(.width(32)) u_R24 (.D(Output), .en(L24), .Q(R24), .clk(in_8), .clr(RESET));
  Register #(.width(32)) R14_2 (.D(Output), .en(L24), .Q(R24), .clk(in_8), .clr(RESET));
  Register #(.width(32)) u_R25 (.D(R20), .en(L25[0]), .Q(R25), .clk(in_8), .clr(RESET));
  Register #(.width(32)) u_R26 (.D(L5), .en(L26), .Q(R26), .clk(in_8), .clr(RESET));
  Register #(.width(32)) u_R27 (.D(LoIn), .en(L27), .Q(R27), .clk(in_8), .clr(RESET));
  Register #(.width(32)) u_R28 (.D(HiIn), .en(L28), .Q(R28), .clk(in_8), .clr(RESET));
  Register #(.width(32)) R28_2 (.D(HiIn), .en(L28), .Q(R28), .clk(in_8), .clr(RESET));
  Register #(.width(32)) u_R29 (.D(in_5), .en(L29), .Q(R29), .clk(in_8), .clr(RESET));
  Register #(.width(32)) u_R31 (.D(in_5), .en(L31), .Q(R31), .clk(in_8), .clr(undriven_4));
  Multiplexer #(.select(5), .width(32)) multiplexer_1 (
    .in0({32{1'b0}}), .in1(R1), .in2(R2), .in3(R3), .in4(R4), .in5(R5), .in6(R6), .in7(R7), .in8(R8),
    .in9(R9), .in10(R5), .in11(in_5), .in12(R12), .in13(R13), .in14(L14), .in15(R15), .in16(R16), .in17(R17),
    .in18(R18), .in19(L25), .in20(R20), .in21(R21), .in22(R22), .in23(R23), .in24(R24), .in25(R25),
    .in26(R26), .in27(R27), .in28(R28), .in29(R29), .in30(R30), .out(Output), .sel(in_1));  // open: in31, en
  Multiplexer #(.select(5), .width(32)) multiplexer_2 (
    .in0({32{1'b0}}), .in1(R1), .in2(R2), .in3({32{1'b0}}), .in4(R4), .in5(R5), .in6(R6), .in7(R7), .in8(R8),
    .in9(R9), .in10(R10), .in11(in_5), .in12(R12), .in13(R17), .in14(R14), .in15(R15), .in16(R23),
    .in17(R18), .in18(R18), .in19(R1), .in20(R20), .in21(R21), .in22(R22), .in23(R23), .in24(R1), .in25(R25),
    .in26(R26), .in27(R27), .in28(R28), .in29(R29), .in30(R30), .out(Output_2), .sel(in_2));  // open: in31, en
  // Pins of 1 and 32 bits meet at in_5
  // Pins of 1 and 32 bits meet at L5
  // Pins of 1 and 32 bits meet at L21
  // Pins of 1 and 5 bits meet at in_2
  // Pins of 1 and 32 bits meet at L20
  // Pins of 1 and 32 bits meet at L14
  // Pins of 1 and 32 bits meet at L25
  // Pins of 1 and 32 bits meet at L3

  assign RW = in_6;
  assign WD = in_5;

  // Other names for the same wires on the sheet: CLOCK = in_8; DA[31:0] = Output; DB[31:0] = Output_2;
  //   R11[31:0] = in_5; R19[31:0] = R1; RR1[4:0] = in_1; RR2[4:0] = in_2; WR[4:0] = in_3
endmodule

module Spliter (
  output [4:0] r,
  output [4:0] out_2,
  output [4:0] out_3,
  output [4:0] out_4,
  output [5:0] out_5,
  output [31:0] Unsigned,
  output [31:0] Signed,
  output [25:0] out_8
);

  wire [31:31] Instruction;

  assign Unsigned = {{16{1'b0}}, {out_8[15:6], out_5}};  // Bit_Extender bit_extender_1
  assign Signed = {{16{out_8[15]}}, {out_8[15:6], out_5}};  // Bit_Extender bit_extender_2
  // Pins of 16 and 26 bits meet at {out_2, out_8[20:6], out_5}
  // Pins of 26 and 28 bits meet at {r[1:0], out_2, out_8[20:6], out_5}
  // Pins of 5 and 6 bits meet at {Instruction[31], r}

  assign out_3 = out_2;
  assign {out_8[25:21], out_8[5:0]} = {out_2, out_5};

  // Other names for the same wires on the sheet: Const[25:0] = {out_2, out_8[20:6], out_5}; FuncCode[5:0] = out_5;
  //   Instruction[30:0] = {r, out_2, out_8[20:6], out_5}; Target[27:0] = {r[1:0], out_2, out_8[20:6], out_5};
  //   RD[4:0] = out_8[15:11]; RT[4:0] = out_8[20:16]; RS[4:0] = out_2; OP_Code[5:0] = {Instruction[31], r}
endmodule
