// Logisim project s-mips.circ as structural Verilog
module S_MIPS_Board (
  input  DESHABILITAR_DISPATCHER,
  output halt
);

  wire button_1_out, CLK, CS, d_ff_1_q, LCLR, LoadRAM, LoadRAMOn, LW, R_R_W, R_W, ram_dispatcher_1_finished,
       RCS, Reset_out, RST, TTY_EN;
  wire [2:0] KDB;
  wire [3:0] LMask, Mask, ram_1_read_time, ram_1_write_time, RMask;
  wire [6:0] KDB_DATA, TTY_DATA;
  wire [15:0] Addr, LAddr, RAddr;
  wire [31:0] I0, I1, I2, I3, LData, ram_1_data_out_0, ram_1_data_out_1, ram_1_data_out_2, ram_1_data_out_3,
       RI0, RI1, RI2, RI3, s_mips_1_output, s_mips_1_pc;

  TTY #(.rows(25), .cols(80)) tty_1 (.data(TTY_DATA), .clk(CLK), .we(TTY_EN), .clr(RST));
  not not_1 (LoadRAMOn, ram_dispatcher_1_finished);
  RAM_Dispatcher ram_dispatcher_1 (
    .WriteTime(ram_1_write_time), .Clock(CLK), .Data(LData), .Address(LAddr), .Mask(LMask),
    .Finished(ram_dispatcher_1_finished), .Write(LW), .CLR(LCLR));
  Keyboard #(.buflen(64)) keyboard_1 (.clk(CLK), .re(KDB[0]), .clr(KDB[1]), .avail(KDB[2]), .data(KDB_DATA));
  // Probe on RAddr
  // Probe on ram_1_data_out_0
  RAM ram_1 (
    .Address(RAddr), .Data_Out_0(ram_1_data_out_0), .Data_Out_1(ram_1_data_out_1),
    .Data_Out_2(ram_1_data_out_2), .Data_Out_3(ram_1_data_out_3), .Data_In_0(RI0), .Data_In_1(RI1),
    .Data_In_2(RI2), .Data_In_3(RI3), .Mask(RMask), .nRead_Write(R_R_W), .Chip_Select(RCS),
    .Read_Time(ram_1_read_time), .Reset(button_1_out), .Write_Time(ram_1_write_time), .in_2(CLK));
  // Probe on ram_1_data_out_1
  Button button_1 (.out(button_1_out));
  D_Flip_Flop d_ff_1 (.clk(CLK), .D(1'b1), .Q(d_ff_1_q), .reset(Reset_out));  // open: Qn, preset, en
  Button Reset (.out(Reset_out));
  S_MIPS s_mips_1 (
    .Kbd_Enable(KDB[0]), .Address(Addr), .Kbd_Clear(KDB[1]), .Kbd_Available(KDB[2]), .RAM_In_0(I0),
    .Kbd_ASCII_Data(KDB_DATA), .RAM_In_1(I1), .TTY_Enable(TTY_EN), .RAM_In_2(I2), .RAM_In_3(I3),
    .TTY_ASCII_Data(TTY_DATA), .Reset(RST), .RAM_Out_0(ram_1_data_out_0), .Clock(CLK),
    .RAM_Out_1(ram_1_data_out_1), .Stop(halt), .RAM_Out_2(ram_1_data_out_2), .RAM_Out_3(ram_1_data_out_3),
    .Mask(Mask), .Read_Time(ram_1_read_time), .Write_Time(ram_1_write_time), .nRead_Write(R_W),
    .Chip_Select(CS), .pc(s_mips_1_pc), .Output(s_mips_1_output));
  D_Flip_Flop d_ff_2 (.clk(CLK), .D(d_ff_1_q), .Qn(LCLR), .reset(Reset_out));  // open: Q, preset, en
  // Probe on ram_1_data_out_2
  or or_1 (RST, LCLR, LoadRAM);
  // Probe on ram_1_data_out_3
  // Probe on s_mips_1_pc
  Clock clock_1 (.out(CLK));
  // Probe on s_mips_1_output
  Multiplexer #(.width(32), .enable("false")) multiplexer_1 (.in0(I0), .in1(LData), .out(RI0), .sel(LoadRAM));
  Multiplexer #(.width(32), .enable("false")) multiplexer_2 (.in0(I1), .in1(LData), .out(RI1), .sel(LoadRAM));
  Multiplexer #(.width(32), .enable("false")) multiplexer_3 (.in0(I2), .in1(LData), .out(RI2), .sel(LoadRAM));
  Multiplexer #(.width(32), .enable("false")) multiplexer_4 (.in0(I3), .in1(LData), .out(RI3), .sel(LoadRAM));
  and and_1 (LoadRAM, ~DESHABILITAR_DISPATCHER, LoadRAMOn);  // AND_Gate
  Multiplexer #(.width(16), .enable("false")) multiplexer_5 (.in0(Addr), .in1(LAddr), .out(RAddr), .sel(LoadRAM));
  Multiplexer #(.width(4), .enable("false")) multiplexer_6 (.in0(Mask), .in1(LMask), .out(RMask), .sel(LoadRAM));
  Multiplexer #(.enable("false")) multiplexer_7 (.in0(CS), .in1(LW), .out(RCS), .sel(LoadRAM));
  Multiplexer #(.enable("false")) multiplexer_8 (.in0(R_W), .in1(LW), .out(R_R_W), .sel(LoadRAM));

  // Notes on the sheet:
  //   NO MODIFICAR
  //   Keyboard
endmodule

module RAM (
  input  [15:0] Address,
  input  in_2,
  input  [31:0] Data_In_0,
  input  [31:0] Data_In_1,
  input  [31:0] Data_In_2,
  input  [31:0] Data_In_3,
  input  [3:0] Mask,
  input  nRead_Write,
  input  Chip_Select,
  input  Reset,
  output [31:0] Data_Out_0,
  output [31:0] Data_Out_1,
  output [31:0] Data_Out_2,
  output [31:0] Data_Out_3,
  output [3:0] Read_Time,
  output [3:0] Write_Time
);

  wire and_2_out, and_3_out, and_4_out, and_5_out, and_6_out, and_7_out, and_8_out, and_9_out, Changed,
       comparator_2_eq, comparator_3_eq, comparator_4_eq, comparator_5_eq, comparator_6_eq, Count,
       demultiplexer_3_out0, Idle, Idle_q, Load, Load0, Load1, nand_1_out, or_1_out, or_2_out, or_3_out,
       or_4_out, or_5_out, or_6_out, or_7_out, or_8_out, or_9_out, or_10_out, Proc_q, Update_Mem, Zero_Time;
  wire [3:0] counter_1_q, multiplexer_1_out, subtractor_1_out;
  wire [31:0] register_1_q, register_2_q, register_3_q, register_4_q, register_5_q;

  // Probe on 4'b0011
  // Probe on 4'b0010
  Multiplexer #(.width(4), .enable("false")) multiplexer_1 (
    .in0(4'b0011), .in1(4'b0010), .out(multiplexer_1_out), .sel(nRead_Write));
  or or_1 (or_1_out, Idle, Update_Mem);
  or or_2 (or_2_out, ~Chip_Select, Reset);  // OR_Gate
  Subtractor #(.width(4)) subtractor_1 (.a(multiplexer_1_out), .b(4'b0010), .out(subtractor_1_out));  // open: bin, bout
  Demultiplexer #(.enable("false")) demultiplexer_1 (.out0(Idle), .out1(Load0), .in(Idle_q), .sel(Changed));
  D_Flip_Flop u_Idle (.clk(in_2), .D(or_1_out), .Q(Idle_q), .preset(or_2_out));  // open: Qn, en, reset
  // Probe on counter_1_q
  Counter #(.width(4), .max('hf)) counter_1 (
    .load(Load), .D(subtractor_1_out), .count(Count), .Q(counter_1_q), .clk(in_2), .clr(or_3_out));  // open: carry
  or or_3 (or_3_out, ~Chip_Select, Reset);  // OR_Gate
  Comparator #(.width(4), .mode("unsigned")) comparator_1 (
    .a(4'b0000), .b(counter_1_q), .eq(Zero_Time));  // open: gt, lt
  or or_4 (or_4_out, Count, Load0, Load1);
  Register #(.width(32)) register_1 (.D(Data_In_0), .en(Chip_Select), .Q(register_1_q), .clk(in_2), .clr(or_5_out));
  or or_5 (or_5_out, ~Chip_Select, Reset);  // OR_Gate
  Register #(.width(32)) register_2 (.D(Data_In_1), .en(Chip_Select), .Q(register_2_q), .clk(in_2), .clr(or_6_out));
  or or_6 (or_6_out, ~Chip_Select, Reset);  // OR_Gate
  Register #(.width(32)) register_3 (.D(Data_In_2), .en(Chip_Select), .Q(register_3_q), .clk(in_2), .clr(or_7_out));
  or or_7 (or_7_out, ~Chip_Select, Reset);  // OR_Gate
  Register #(.width(32)) register_4 (.D(Data_In_3), .en(Chip_Select), .Q(register_4_q), .clk(in_2), .clr(or_8_out));
  or or_8 (or_8_out, ~Chip_Select, Reset);  // OR_Gate
  Register #(.width(32)) register_5 (
    .D({{11{1'b1}}, nRead_Write, Mask, Address}), .en(Chip_Select), .Q(register_5_q), .clk(in_2),
    .clr(or_9_out));
  or or_9 (or_9_out, ~Chip_Select, Reset);  // OR_Gate
  D_Flip_Flop Proc (.clk(in_2), .D(or_4_out), .Q(Proc_q), .reset(or_10_out));  // open: Qn, preset, en
  or or_10 (or_10_out, ~Chip_Select, Reset);  // OR_Gate
  Demultiplexer #(.enable("false")) demultiplexer_2 (
    .out0(Count), .out1(Update_Mem), .in(demultiplexer_3_out0), .sel(Zero_Time));
  Demultiplexer #(.enable("false")) demultiplexer_3 (
    .out0(demultiplexer_3_out0), .out1(Load1), .in(Proc_q), .sel(Changed));
  Clock clock_1 ();  // open: out
  Comparator #(.width(32)) comparator_2 (.a(register_1_q), .b(Data_In_0), .eq(comparator_2_eq));  // open: gt, lt
  Comparator #(.width(32)) comparator_3 (.a(register_2_q), .b(Data_In_1), .eq(comparator_3_eq));  // open: gt, lt
  Comparator #(.width(32)) comparator_4 (.a(register_3_q), .b(Data_In_2), .eq(comparator_4_eq));  // open: gt, lt
  Comparator #(.width(32)) comparator_5 (.a(register_4_q), .b(Data_In_3), .eq(comparator_5_eq));  // open: gt, lt
  Comparator #(.width(32)) comparator_6 (
    .a(register_5_q), .b({{11{1'b1}}, nRead_Write, Mask, Address}), .eq(comparator_6_eq));  // open: gt, lt
  nand nand_1 (nand_1_out, comparator_6_eq, comparator_2_eq, comparator_3_eq, comparator_4_eq, comparator_5_eq);
  and and_1 (Changed, nand_1_out, Chip_Select);
  or or_11 (Load, Count, Load1, Load0);
  and and_2 (and_2_out, Mask[0], Update_Mem, nRead_Write);
  and and_3 (and_3_out, Mask[1], Update_Mem, nRead_Write);
  and and_4 (and_4_out, Mask[2], Update_Mem, nRead_Write);
  and and_5 (and_5_out, Mask[3], Update_Mem, nRead_Write);
  RAM_part #(.addrWidth(16), .dataWidth(32), .bus("separate")) ram_1 (
    .addr(Address), .din(Data_In_0), .data(Data_Out_0), .str(and_2_out), .sel(Chip_Select), .clk(in_2),
    .ld(and_6_out), .clr(Reset));
  and and_6 (and_6_out, ~nRead_Write, Idle);  // AND_Gate
  RAM_part #(.addrWidth(16), .dataWidth(32), .bus("separate")) ram_2 (
    .addr(Address), .din(Data_In_1), .data(Data_Out_1), .str(and_3_out), .sel(Chip_Select), .clk(in_2),
    .ld(and_7_out), .clr(Reset));
  and and_7 (and_7_out, ~nRead_Write, Idle);  // AND_Gate
  RAM_part #(.addrWidth(16), .dataWidth(32), .bus("separate")) ram_3 (
    .addr(Address), .din(Data_In_2), .data(Data_Out_2), .str(and_4_out), .sel(Chip_Select), .clk(in_2),
    .ld(and_8_out), .clr(Reset));
  and and_8 (and_8_out, ~nRead_Write, Idle);  // AND_Gate
  RAM_part #(.addrWidth(16), .dataWidth(32), .bus("separate")) ram_4 (
    .addr(Address), .din(Data_In_3), .data(Data_Out_3), .str(and_5_out), .sel(Chip_Select), .clk(in_2),
    .ld(and_9_out), .clr(Reset));
  and and_9 (and_9_out, ~nRead_Write, Idle);  // AND_Gate

  assign Read_Time = 4'b0011;
  assign Write_Time = 4'b0010;

  // Other names for the same wires on the sheet: M0 = Mask[0]; M1 = Mask[1]; M2 = Mask[2]; M3 = Mask[3];
  //   RW = nRead_Write; CLK = in_2; CLR = Reset; CS = Chip_Select; Load2 = Count

  // Notes on the sheet:
  //   NO MODIFICAR
  //   excepto quizás los valores RT y WT
  //   BANK0
  //   BANK1
  //   BANK2
  //   BANK3
endmodule

module S_MIPS (
  input  Kbd_Available,
  input  [6:0] Kbd_ASCII_Data,
  input  [31:0] RAM_Out_0,
  input  [31:0] RAM_Out_1,
  input  Reset,
  input  [31:0] RAM_Out_2,
  input  Clock,
  input  [31:0] RAM_Out_3,
  input  [3:0] Read_Time,
  input  [3:0] Write_Time,
  output Kbd_Enable,
  output [15:0] Address,
  output Kbd_Clear,
  output TTY_Enable,
  output [6:0] TTY_ASCII_Data,
  output Stop,
  output [31:0] RAM_In_0,
  output [31:0] Output,
  output [31:0] RAM_In_1,
  output [31:0] RAM_In_2,
  output [31:0] RAM_In_3,
  output [31:0] pc,
  output [3:0] Mask,
  output nRead_Write,
  output Chip_Select
);

  wire A1S0, A2S0, A2S1, and_1_out, CacheWrite, HALT, Hit, HitInC, isValid, isValidInst, LCacheOut, LHI_LO,
       LimitCycles, LInstCache, LPC, LpcOut, LRegOut, LSP, LSPOut, LValid, LValidInst, Ms0, Ms1, not_1_out,
       On, RamAdds, RaR, Raw, RW, WDS0, WDS1;
  wire [1:0] RAMinS;
  wire [2:0] AluOP;
  wire [31:0] counterCicles, DataCache_setdata, DataCacheO, datapath_1_ram_wdata, InstructionCache_setdata,
       PC_prime, RamAdd, RamAdd_t, RamWData;

  not not_1 (not_1_out, HALT);
  Demultiplexer #(.select(2), .width(32)) demultiplexer_1 (
    .out0(RAM_In_0), .out1(RAM_In_1), .out2(RAM_In_2), .out3(RAM_In_3), .in(RamWData), .sel(RAMinS));  // open: en
  Multiplexer #(.width(32)) multiplexer_1 (.in0(pc), .in1(RamAdd_t), .out(RamAdd), .sel(RamAdds));  // open: en
  D_Flip_Flop #(.trigger("falling")) d_ff_1 (
    .clk(Clock), .D(not_1_out), .Q(On), .en(1'b1), .reset(Reset));  // open: Qn, preset
  RamDecoder ramdecoder_1 (.BRUTE_RAMADD(RamAdd), .RAM_MASK(Mask), .RAM_IN_SEL(RAMinS), .RAM_ADD_REAL(Address));
  Counter #(.width(32), .max('hffffffff)) counter_1 (
    .count(Clock), .Q(counterCicles), .clk(Clock), .clr(Reset));  // open: load, D, carry
  Comparator #(.width(32)) comparator_1 (.a(counterCicles), .b(32'hf4240), .gt(LimitCycles));  // open: eq, lt
  or or_1 (Stop, HALT, LimitCycles);
  and and_1 (and_1_out, On, HitInC);
  ControlUnit_2 controlunit_1 (
    .RW(RW), .LPC(LPC), .Instruction(Output), .SP_LO(LSP), .HI_LO(LHI_LO), .on(and_1_out), .A1S0(A1S0),
    .A2S1(A2S1), .A2S0(A2S0), .WDS1(WDS1), .WDS0(WDS0), .RAR(RaR), .RAW(Raw), .Ms1(Ms1), .Ms0(Ms0),
    .TTY_EN(TTY_Enable), .Halt(HALT), .KBD_EN(Kbd_Enable), .ALUOP(AluOP));  // open: A1S1
  Multiplexer #(.width(32)) multiplexer_2 (.in0(pc), .in1(RamAdd_t), .out(PC_prime), .sel(CacheWrite));  // open: en
  Cache_2 DataCache (
    .HIT(Hit), .Adress(RamAdd_t), .SetData(DataCache_setdata), .Clock(Clock), .isValid(isValid),
    .RESET(Reset), .MemoryData0(RAM_Out_0), .MemoryData1(RAM_Out_1), .MemoryData2(RAM_Out_2),
    .MemoryData3(RAM_Out_3), .RW(LCacheOut), .Valided(LValid), .DataWrite(RamWData), .RamWrite(CacheWrite));
  Cache_2 InstructionCache (
    .HIT(HitInC), .Adress(pc), .SetData(InstructionCache_setdata), .Clock(Clock), .isValid(isValidInst),
    .RESET(Reset), .MemoryData0(RAM_Out_0), .MemoryData1(RAM_Out_1), .MemoryData2(RAM_Out_2),
    .MemoryData3(RAM_Out_3), .RW(LInstCache), .Valided(LValidInst), .DataWrite(RamWData), .RamWrite(1'b0));
  // Probe on InstructionCache_setdata
  RAM_TRANSLATE ram_translate_1 (.RAM_IN(DataCache_setdata), .TRANSLATED(DataCacheO));
  // Probe on DataCacheO
  RAM_TRANSLATE ram_translate_2 (.RAM_IN(InstructionCache_setdata), .TRANSLATED(Output));
  RAMUI ramui_1 (
    .HIT(Hit), .RamRead(RaR), .WriteRam(Raw), .CLk(Clock), .LoPCin(LPC), .LoRegin(RW), .LoSP(LSP),
    .RRT(Read_Time), .WRT(Write_Time), .RST(Reset), .LoadCache(LCacheOut), .LoPC(LpcOut), .LoReg(LRegOut),
    .LoSP_2(LSPOut), .HitInsCache(HitInC), .LoadInstCache(LInstCache), .RamAddS(RamAdds),
    .RamUse(Chip_Select), .RamWrite(nRead_Write), .isValid(isValid), .LValid(LValid),
    .isValidInst(isValidInst), .LValidInst(LValidInst), .PC(pc), .ON(On), .RST_2(Reset),
    .CacheWrite(CacheWrite));
  DataPath datapath_1 (
    .instruct(Output), .CLK(Clock), .RW(LRegOut), .RAM_Rdata(DataCacheO), .RAM_Wdata(datapath_1_ram_wdata),
    .LPC(LpcOut), .RSTPC(Reset), .RSTRF(Reset), .LSP(LSPOut), .LHi_Lo(LHI_LO), .ALUOP(AluOP), .PC(pc),
    .RAM_Add(RamAdd_t), .ALU1S(A1S0), .AS1(A2S1), .AS0(A2S0), .WDS0(WDS0), .WDS1(WDS1), .MS0(Ms0), .MS1(Ms1),
    .TTY_DATA(TTY_ASCII_Data), .KB_DATA(Kbd_ASCII_Data), .KB_AVAIL(Kbd_Available));
  RAM_TRANSLATE ram_translate_3 (.RAM_IN(datapath_1_ram_wdata), .TRANSLATED(RamWData));
  // Probe on RW
  // Probe on LPC
  // Probe on LSP
  // Probe on LHI_LO
  // Probe on A1S0
  // Probe on A2S1
  // Probe on A2S0
  // Probe on WDS1
  // Probe on WDS0
  // Probe on RaR
  // Probe on Raw
  // Probe on Ms1
  // Probe on Ms0
  // Probe on AluOP
  // Probe on TTY_Enable
  // Probe on HALT
  // Probe on Kbd_Enable
  // Probe on Output
  // Probe on RAM_Out_0
  // Probe on RAM_Out_1
  // Probe on RAM_Out_2
  // Probe on RAM_Out_3
  // Probe on Read_Time
  // Probe on Write_Time
  // Probe on Hit
  // Probe on isValid
  // Probe on HitInC
  // Probe on isValidInst
  // Probe on RamAdd_t
  // Probe on RamAdd
  // Probe on pc
  // Probe on TTY_ASCII_Data
  // Probe on Kbd_ASCII_Data
  // Probe on Kbd_Available
  // Probe on RamAdds
  // Probe on Chip_Select
  // Probe on LInstCache
  // Probe on nRead_Write
  // Probe on LpcOut
  // Probe on LCacheOut
  // Probe on LRegOut
  // Probe on LSPOut
  // Probe on LValid
  // Probe on LValidInst
  // Probe on RamWData
  // Probe on Reset
  // Probe on Clock

  assign Kbd_Clear = Reset;

  // Other names for the same wires on the sheet: CLK = Clock; Instruction[31:0] = Output; KBD_AVAIL = Kbd_Available;
  //   KBD_DATA[6:0] = Kbd_ASCII_Data; RAM_A[15:0] = Address; RAM_INPUT_0[31:0] = RAM_In_0;
  //   RAM_INPUT_1[31:0] = RAM_In_1; RAM_INPUT_2[31:0] = RAM_In_2; RAM_INPUT_3[31:0] = RAM_In_3; RAM_MASK[3:0] = Mask;
  //   RAM_OUTPUT_0[31:0] = RAM_Out_0; RAM_OUTPUT_1[31:0] = RAM_Out_1; RAM_OUTPUT_2[31:0] = RAM_Out_2;
  //   RAM_OUTPUT_3[31:0] = RAM_Out_3; RamUse = Chip_Select; RamWrite = nRead_Write; KBD_CLR = Reset; RST = Reset;
  //   TTY_DATA[6:0] = TTY_ASCII_Data

  // Notes on the sheet:
  //   RAM ADDRESS
  //   DATA FROM RAM
  //   DATA TO RAM
  //   DATA WRITE MASK
  //   RAM TIMING
  //   RAM CONTROL
  //   KEYBOARD
  //   TTY
  //   SEQUENCING
endmodule

module RAM_Dispatcher (
  input  [3:0] WriteTime,
  input  Clock,
  input  CLR,
  output [31:0] Data,
  output [15:0] Address,
  output [3:0] Mask,
  output Finished,
  output Write
);

  wire demultiplexer_2_out1, demultiplexer_3_out1, End, IDLE_q, IncAddr, Load, or_1_out, or_2_out, While_q,
       WriteEnd;
  wire [3:0] counter_1_q;
  wire [31:0] CurrentAddress_q;

  Counter #(.width(32), .max('hffffffff)) CurrentAddress (
    .count(IncAddr), .Q({CurrentAddress_q[31:18], Address, CurrentAddress_q[1:0]}), .clk(Clock), .clr(CLR));  // open: load, D, carry
  or or_1 (or_1_out, IncAddr, demultiplexer_3_out1, Finished);
  D_Flip_Flop IDLE (.clk(Clock), .D(or_1_out), .Q(IDLE_q), .preset(CLR));  // open: Qn, en, reset
  Demultiplexer #(.enable("false")) demultiplexer_1 (.out0(Load), .out1(Finished), .in(IDLE_q), .sel(End));
  D_Flip_Flop While (.clk(Clock), .D(or_2_out), .Q(While_q), .reset(CLR));  // open: Qn, preset, en
  or or_2 (or_2_out, Write, Load);
  RAM_part #(.addrWidth(18), .dataWidth(32)) ram_1 (
    .addr({Address, CurrentAddress_q[1:0]}), .data(Data), .clk(Clock));  // open: sel, ld, clr
  Demultiplexer #(.enable("false")) demultiplexer_2 (
    .out0(Write), .out1(demultiplexer_2_out1), .in(While_q), .sel(WriteEnd));
  Decoder #(.select(2)) decoder_1 (
    .out0(Mask[0]), .out1(Mask[1]), .out2(Mask[2]), .out3(Mask[3]), .sel(CurrentAddress_q[1:0]));  // open: en
  Demultiplexer #(.enable("false")) demultiplexer_3 (
    .out0(IncAddr), .out1(demultiplexer_3_out1), .in(demultiplexer_2_out1), .sel(End));
  Counter #(.width(4), .max('hf)) counter_1 (
    .load(Load), .D(WriteTime), .count(Write), .Q(counter_1_q), .clk(Clock));  // open: carry, clr
  Comparator #(.width(32)) comparator_1 (.a(Data), .b({32{1'b1}}), .eq(End));  // open: gt, lt
  Comparator #(.width(4)) comparator_2 (.a(4'b0000), .b(counter_1_q), .eq(WriteEnd));  // open: gt, lt

  // Other names for the same wires on the sheet: CLK = Clock; Count = Write; WT[3:0] = WriteTime
endmodule

module ALU (
  input  [31:0] op0,
  input  [31:0] op1,
  input  [2:0] op_code,
  input  [1:0] MD_code,
  output [31:0] Result,
  output isZero,
  output isNegative,
  output [31:0] Lo,
  output [31:0] Hi
);

  wire comparator_1_lt, comparator_2_lt;
  wire [31:0] Add, And, DivHi, DivLo, DivuHi, DivuLo, MultHi, MultLo, MuluHi, MuluLo, Nor, Or, Slt, Sltu,
       Sub, Xor;

  Mult mult_1 (.in_1(op0), .in_2(op1), .Lo(MultLo), .Hi(MultHi));
  Multiplier #(.width(32)) multiplier_1 (.a(op0), .b(op1), .out(MuluLo), .cout(MuluHi));  // open: cin
  Div div_1 (.in_1(op0), .in_2(op1), .Lo(DivLo), .Hi(DivHi));
  Divider #(.width(32)) divider_1 (.a(op0), .b(op1), .out(DivuLo), .rem(DivuHi));  // open: upper
  Adder #(.width(32)) adder_1 (.a(op0), .b(op1), .out(Add));  // open: cin, cout
  Subtractor #(.width(32)) subtractor_1 (.a(op0), .b(op1), .out(Sub));  // open: bin, bout
  assign And = op0 & op1;  // AND_Gate and_1, 32 bits wide
  assign Or = op0 | op1;  // OR_Gate or_1, 32 bits wide
  assign Nor = ~(op0 | op1);  // NOR_Gate nor_1, 32 bits wide
  assign Xor = op0 ^ op1;  // XOR_Gate xor_1, 32 bits wide
  Comparator #(.width(32)) comparator_1 (.a(op0), .b(op1), .lt(comparator_1_lt));  // open: gt, eq
  Comparator #(.width(32), .mode("unsigned")) comparator_2 (.a(op0), .b(op1), .lt(comparator_2_lt));  // open: gt, eq
  assign Slt = {{31{1'b0}}, comparator_1_lt};  // Bit_Extender bit_extender_1
  assign Sltu = {{31{1'b0}}, comparator_2_lt};  // Bit_Extender bit_extender_2
  Multiplexer #(.select(3), .width(32)) multiplexer_1 (
    .in0(Add), .in1(Sub), .in2(And), .in3(Or), .in4(Nor), .in5(Xor), .in6(Slt), .in7(Sltu), .out(Result),
    .sel(op_code));  // open: en
  Multiplexer #(.select(2), .width(32)) multiplexer_2 (
    .in0(MultLo), .in1(MuluLo), .in2(DivLo), .in3(DivuLo), .out(Lo), .sel(MD_code));  // open: en
  Multiplexer #(.select(2), .width(32)) multiplexer_3 (
    .in0(MultHi), .in1(MuluHi), .in2(DivHi), .in3(DivuHi), .out(Hi), .sel(MD_code));  // open: en
  Comparator #(.width(32)) comparator_3 (.a(Result), .b({32{1'b0}}), .eq(isZero), .lt(isNegative));  // open: gt

  // Other names for the same wires on the sheet: A[31:0] = op0; B[31:0] = op1; MD[1:0] = MD_code; OP[2:0] = op_code

  // Notes on the sheet:
  //   Op-index
  //   Add-----000
  //   Sub-----001
  //   And-----010
  //   Or-----011
  //   Nor-----100
  //   Xor-----101
  //   Slt-----110
  //   Sltu-----111
  //   Mult-----00
  //   Mulu-----01
  //   Div-----10
  //   Divu-----11
endmodule

module Mult (
  input  [31:0] in_1,
  input  [31:0] in_2,
  output [31:0] Lo,
  output [31:0] Hi
);

  wire adder_1_cout, Sign, tounsigned_1_sign, tounsigned_2_sign;
  wire [31:0] HiN, HiP, LoN, LoP, not_1_out, not_2_out, tounsigned_1_x, tounsigned_2_x;

  // Probe on in_1
  // Probe on in_2
  ToUnsigned tounsigned_1 (.in_1(in_1), .x(tounsigned_1_x), .Sign(tounsigned_1_sign));
  ToUnsigned tounsigned_2 (.in_1(in_2), .x(tounsigned_2_x), .Sign(tounsigned_2_sign));
  xor xor_1 (Sign, tounsigned_1_sign, tounsigned_2_sign);
  Multiplexer #(.width(32)) multiplexer_1 (.in0(LoP), .in1(LoN), .out(Lo), .sel(Sign));  // open: en
  Multiplexer #(.width(32)) multiplexer_2 (.in0(HiP), .in1(HiN), .out(Hi), .sel(Sign));  // open: en
  Multiplier #(.width(32)) multiplier_1 (.a(tounsigned_1_x), .b(tounsigned_2_x), .out(LoP), .cout(HiP));  // open: cin
  // Probe on Lo
  // Probe on Hi
  assign not_1_out = ~LoP;  // NOT_Gate not_1, 32 bits wide
  assign not_2_out = ~HiP;  // NOT_Gate not_2, 32 bits wide
  Adder #(.width(32)) adder_1 (.a(not_1_out), .b(32'h1), .out(LoN), .cout(adder_1_cout));  // open: cin
  Adder #(.width(32)) adder_2 (.a(not_2_out), .b({32{1'b0}}), .out(HiN), .cin(adder_1_cout));  // open: cout

  // Other names for the same wires on the sheet: A[31:0] = in_1; B[31:0] = in_2
endmodule

module Div (
  input  [31:0] in_1,
  input  [31:0] in_2,
  output [31:0] Lo,
  output [31:0] Hi
);

  wire Sign;
  wire [1:0] HiS;
  wire [31:0] Hi1, Hi2, Hi3, LoN, LoP, mult_1_lo, mult_2_lo, not_1_out, tounsigned_1_x, tounsigned_2_x;

  // Probe on in_1
  // Probe on in_2
  ToUnsigned tounsigned_1 (.in_1(in_1), .x(tounsigned_1_x), .Sign(HiS[0]));
  ToUnsigned tounsigned_2 (.in_1(in_2), .x(tounsigned_2_x), .Sign(HiS[1]));
  Mult mult_1 (.in_1(in_2), .in_2(LoN), .Lo(mult_1_lo));  // open: Hi
  Mult mult_2 (.in_1(in_2), .in_2(LoP), .Lo(mult_2_lo));  // open: Hi
  Subtractor #(.width(32)) subtractor_1 (.a(in_1), .b(mult_1_lo), .out(Hi2));  // open: bin, bout
  Subtractor #(.width(32)) subtractor_2 (.a(in_1), .b(mult_2_lo), .out(Hi3));  // open: bin, bout
  Divider #(.width(32)) divider_1 (.a(tounsigned_1_x), .b(tounsigned_2_x), .out(LoP), .rem(Hi1));  // open: upper
  assign not_1_out = ~LoP;  // NOT_Gate not_1, 32 bits wide
  // Probe on Lo
  // Probe on Hi
  Multiplexer #(.width(32)) multiplexer_1 (.in0(LoP), .in1(LoN), .out(Lo), .sel(Sign));  // open: en
  Multiplexer #(.select(2), .width(32)) multiplexer_2 (
    .in0(Hi1), .in1(Hi2), .in2(Hi2), .in3(Hi3), .out(Hi), .sel(HiS));  // open: en
  Adder #(.width(32)) adder_1 (.a(not_1_out), .b(32'h1), .out(LoN));  // open: cin, cout
  xor xor_1 (Sign, HiS[0], HiS[1]);

  // Other names for the same wires on the sheet: A[31:0] = in_1; B[31:0] = in_2; SignA = HiS[0]; SignB = HiS[1]
endmodule

module ToUnsigned (
  input  [31:0] in_1,
  output [31:0] x,
  output Sign
);

  wire [31:0] negator_1_out;

  Negator #(.width(32)) negator_1 (.in(in_1), .out(negator_1_out));
  Multiplexer #(.width(32)) multiplexer_1 (.in0(in_1), .in1(negator_1_out), .out(x), .sel(in_1[31]));  // open: en

  assign Sign = in_1[31];
endmodule

module circuit (
  input  [30:0] A,
  input  [30:0] B,
  output idx,
  output [30:0] out_4,
  output [30:0] out_5
);

  Comparator #(.width(31), .mode("unsigned")) comparator_1 (.a(A), .b(B), .lt(idx));  // open: gt, eq
  Multiplexer #(.width(31)) multiplexer_1 (.in0(A), .in1(B), .out(out_4), .sel(idx));  // open: en
  Multiplexer #(.width(31)) multiplexer_2 (.in0(B), .in1(A), .out(out_5), .sel(idx));  // open: en
endmodule

module RegisterFile (
  input  Clock,
  input  Reset,
  input  RW,
  input  [31:0] SPIn,
  input  Hi_lo_L,
  input  SP_Lo,
  input  [4:0] RR1,
  input  [4:0] RR2,
  input  [4:0] WR,
  input  [31:0] WD,
  input  [31:0] HiIn,
  input  [31:0] LoIn,
  output [31:0] SP,
  output [31:0] Hi,
  output [31:0] Lo,
  output [31:0] DA,
  output [31:0] DB
);

  wire L1, L2, L3, L4, L5, L6, L7, L8, L9, L10, L11, L12, L13, L14, L15, L16, L17, L18, L19, L20, L21, L22,
       L23, L24, L25, L26, L27, L28, L29, L30, L31;
  wire [31:0] R1, R2, R3, R4, R5, R6, R7, R8, R9, R10, R11, R12, R13, R14, R15, R16, R17, R18, R19, R20, R21,
       R22, R23, R24, R25, R26, R27, R28, R29, R30;

  Demultiplexer #(.select(5)) demultiplexer_1 (
    .out1(L1), .out2(L2), .out3(L3), .out4(L4), .out5(L5), .out6(L6), .out7(L7), .out8(L8), .out9(L9),
    .out10(L10), .out11(L11), .out12(L12), .out13(L13), .out14(L14), .out15(L15), .out16(L16), .out17(L17),
    .out18(L18), .out19(L19), .out20(L20), .out21(L21), .out22(L22), .out23(L23), .out24(L24), .out25(L25),
    .out26(L26), .out27(L27), .out28(L28), .out29(L29), .out30(L30), .out31(L31), .in(RW), .sel(WR));  // open: out0, en
  Register #(.width(32)) u_Hi (.D(HiIn), .en(Hi_lo_L), .Q(Hi), .clk(Clock), .clr(Reset));
  Register #(.width(32)) u_Lo (.D(LoIn), .en(Hi_lo_L), .Q(Lo), .clk(Clock), .clr(Reset));
  Register #(.width(32)) u_R1 (.D(WD), .en(L1), .Q(R1), .clk(Clock), .clr(Reset));
  Register #(.width(32)) u_R2 (.D(WD), .en(L2), .Q(R2), .clk(Clock), .clr(Reset));
  Register #(.width(32)) u_R3 (.D(WD), .en(L3), .Q(R3), .clk(Clock), .clr(Reset));
  Register #(.width(32)) u_R4 (.D(WD), .en(L4), .Q(R4), .clk(Clock), .clr(Reset));
  Register #(.width(32)) u_R5 (.D(WD), .en(L5), .Q(R5), .clk(Clock), .clr(Reset));
  Register #(.width(32)) u_R6 (.D(WD), .en(L6), .Q(R6), .clk(Clock), .clr(Reset));
  Register #(.width(32)) u_R7 (.D(WD), .en(L7), .Q(R7), .clk(Clock), .clr(Reset));
  Register #(.width(32)) u_R8 (.D(WD), .en(L8), .Q(R8), .clk(Clock), .clr(Reset));
  Register #(.width(32)) u_R9 (.D(WD), .en(L9), .Q(R9), .clk(Clock), .clr(Reset));
  Register #(.width(32)) u_R10 (.D(WD), .en(L10), .Q(R10), .clk(Clock), .clr(Reset));
  Register #(.width(32)) u_R11 (.D(WD), .en(L11), .Q(R11), .clk(Clock), .clr(Reset));
  Register #(.width(32)) u_R12 (.D(WD), .en(L12), .Q(R12), .clk(Clock), .clr(Reset));
  Register #(.width(32)) u_R13 (.D(WD), .en(L13), .Q(R13), .clk(Clock), .clr(Reset));
  Register #(.width(32)) u_R14 (.D(WD), .en(L14), .Q(R14), .clk(Clock), .clr(Reset));
  Register #(.width(32)) u_R15 (.D(WD), .en(L15), .Q(R15), .clk(Clock), .clr(Reset));
  Register #(.width(32)) u_R16 (.D(WD), .en(L16), .Q(R16), .clk(Clock), .clr(Reset));
  Register #(.width(32)) u_R17 (.D(WD), .en(L17), .Q(R17), .clk(Clock), .clr(Reset));
  Register #(.width(32)) u_R18 (.D(WD), .en(L18), .Q(R18), .clk(Clock), .clr(Reset));
  Register #(.width(32)) u_R19 (.D(WD), .en(L19), .Q(R19), .clk(Clock), .clr(Reset));
  Register #(.width(32)) u_R20 (.D(WD), .en(L20), .Q(R20), .clk(Clock), .clr(Reset));
  Register #(.width(32)) u_R21 (.D(WD), .en(L21), .Q(R21), .clk(Clock), .clr(Reset));
  Register #(.width(32)) u_R22 (.D(WD), .en(L22), .Q(R22), .clk(Clock), .clr(Reset));
  Register #(.width(32)) u_R23 (.D(WD), .en(L23), .Q(R23), .clk(Clock), .clr(Reset));
  Register #(.width(32)) u_R24 (.D(WD), .en(L24), .Q(R24), .clk(Clock), .clr(Reset));
  Register #(.width(32)) u_R25 (.D(WD), .en(L25), .Q(R25), .clk(Clock), .clr(Reset));
  Register #(.width(32)) u_R26 (.D(WD), .en(L26), .Q(R26), .clk(Clock), .clr(Reset));
  Register #(.width(32)) u_R27 (.D(WD), .en(L27), .Q(R27), .clk(Clock), .clr(Reset));
  Register #(.width(32)) u_R28 (.D(WD), .en(L28), .Q(R28), .clk(Clock), .clr(Reset));
  Register #(.width(32)) u_R29 (.D(WD), .en(L29), .Q(R29), .clk(Clock), .clr(Reset));
  Register #(.width(32)) u_R30 (.D(WD), .en(L30), .Q(R30), .clk(Clock), .clr(Reset));
  Register #(.width(32)) R31 (.D(SPIn), .en(SP_Lo), .Q(SP), .clk(Clock), .clr(Reset));
  Multiplexer #(.select(5), .width(32)) multiplexer_1 (
    .in0({32{1'b0}}), .in1(R1), .in2(R2), .in3(R3), .in4(R4), .in5(R5), .in6(R6), .in7(R7), .in8(R8),
    .in9(R9), .in10(R10), .in11(R11), .in12(R12), .in13(R13), .in14(R14), .in15(R15), .in16(R16), .in17(R17),
    .in18(R18), .in19(R19), .in20(R20), .in21(R21), .in22(R22), .in23(R23), .in24(R24), .in25(R25),
    .in26(R26), .in27(R27), .in28(R28), .in29(R29), .in30(R30), .in31(SP), .out(DA), .sel(RR1));  // open: en
  Multiplexer #(.select(5), .width(32)) multiplexer_2 (
    .in0({32{1'b0}}), .in1(R1), .in2(R2), .in3(R3), .in4(R4), .in5(R5), .in6(R6), .in7(R7), .in8(R8),
    .in9(R9), .in10(R10), .in11(R11), .in12(R12), .in13(R13), .in14(R14), .in15(R15), .in16(R16), .in17(R17),
    .in18(R18), .in19(R19), .in20(R20), .in21(R21), .in22(R22), .in23(R23), .in24(R24), .in25(R25),
    .in26(R26), .in27(R27), .in28(R28), .in29(R29), .in30(R30), .in31(SP), .out(DB), .sel(RR2));  // open: en
endmodule

module Spliter (
  input  [31:0] in_1,
  output [5:0] opcode,
  output [2:0] B_Code,
  output [4:0] rs,
  output [4:0] rt,
  output [4:0] rd,
  output [5:0] funccode,
  output [31:0] Unsigned,
  output [31:0] Signed,
  output [25:0] target,
  output Nop
);

  Comparator #(.width(32)) comparator_1 (.a(in_1), .b({32{1'b0}}), .eq(Nop));  // open: gt, lt
  assign Unsigned = {{16{1'b0}}, in_1[15:0]};  // Bit_Extender bit_extender_1
  assign Signed = {{16{in_1[15]}}, in_1[15:0]};  // Bit_Extender bit_extender_2

  assign B_Code = in_1[28:26];
  assign funccode = in_1[5:0];
  assign opcode = in_1[31:26];
  assign rd = in_1[15:11];
  assign rs = in_1[25:21];
  assign rt = in_1[20:16];
  assign target = in_1[25:0];

  // Other names for the same wires on the sheet: Const[15:0] = in_1[15:0]; Instruction[31:0] = in_1;
  //   BCode[2:0] = in_1[28:26]; OP_Code[5:0] = in_1[31:26]
endmodule

module DataPath (
  input  CLK,
  input  RSTRF,
  input  RSTPC,
  input  RW,
  input  LPC,
  input  LSP,
  input  LHi_Lo,
  input  [2:0] ALUOP,
  input  ALU1S,
  input  [31:0] instruct,
  input  [31:0] RAM_Rdata,
  input  AS0,
  input  AS1,
  input  WDS0,
  input  MS0,
  input  WDS1,
  input  MS1,
  input  [6:0] KB_DATA,
  input  KB_AVAIL,
  output [31:0] PC,
  output [6:0] TTY_DATA,
  output [31:0] RAM_Wdata,
  output [31:0] RAM_Add
);

  wire and_2_out, and_4_out, b0_prime, b1_prime, b2_prime, b3_prime, b4_prime, b5_prime, comparator_3_eq,
       comparator_4_eq, EspCase, EspCasePush, IsPoP, IsPopOrPush, IsPush, NF, nop, nor_1_out, not_1_out,
       not_2_out, o0, o1, o2, o3, o4, o5, RAS, wr_sp, ZF;
  wire [1:0] I_Type;
  wire [2:0] B_CODE;
  wire [4:0] RD, RS, RT, WR;
  wire [25:0] Target;
  wire [31:0] ALUI1, ALUI2, ALUR, Const, Hi, HiIn, KB_DATA_t, Lo, LoIn, multiplexer_1_out, multiplexer_5_out,
       multiplexer_9_out, multiplexer_10_out, multiplexer_11_out, RAND, RB, Sconst, SP, Uconst, WD;
  wire [31:7] RA;

  Random #(.width(32)) random_1 (.clk(CLK), .out(RAND));  // open: next, clr
  assign KB_DATA_t = {{25{1'b0}}, KB_DATA};  // Bit_Extender bit_extender_1
  Spliter spliter_1 (
    .in_1(instruct), .opcode({o5, o4, o3, o2, o1, o0}), .B_Code(B_CODE), .rs(RS), .rt(RT), .rd(RD),
    .funccode({b5_prime, b4_prime, b3_prime, b2_prime, b1_prime, b0_prime}), .Unsigned(Uconst),
    .Signed(Sconst), .target(Target), .Nop(nop));
  I_TYPE i_type_1 (.OP_CODE({o5, o4, o3, o2, o1, o0}), .I_Type(I_Type));
  Multiplexer #(.width(32)) multiplexer_1 (
    .in0({RA, TTY_DATA}), .in1(SP), .out(multiplexer_1_out), .sel(ALU1S));  // open: en
  // Probe on {AS1, AS0}
  Multiplexer #(.select(2), .width(32)) multiplexer_2 (
    .in0(RB), .in1(Sconst), .in2(32'h4), .in3({32{1'b0}}), .out(ALUI2), .sel({AS1, AS0}));  // open: en
  Multiplexer #(.width(5)) multiplexer_3 (.in0(RT), .in1(RD), .out(WR), .sel(I_Type[0]));  // open: en
  Multiplexer #(.width(32)) multiplexer_4 (.in0(Sconst), .in1(Uconst), .out(Const), .sel(1'b0));  // open: en
  nor nor_1 (nor_1_out, b5_prime, b5_prime, b5_prime, b5_prime, b5_prime);
  Multiplexer #(.width(32)) multiplexer_5 (
    .in0({RA, TTY_DATA}), .in1(RB), .out(multiplexer_5_out), .sel(not_1_out));  // open: en
  not not_1 (not_1_out, I_Type[0]);
  Multiplexer #(.width(32)) multiplexer_6 (.in0(ALUR), .in1(SP), .out(RAM_Add), .sel(IsPoP));  // open: en
  Multiplexer #(.width(32)) multiplexer_7 (
    .in0(multiplexer_1_out), .in1(RAM_Rdata), .out(ALUI1), .sel(EspCase));  // open: en
  // Probe on WR
  and and_1 (RAS, nor_1_out, b5_prime, I_Type[0]);
  Multiplexer #(.width(32)) multiplexer_8 (
    .in0(multiplexer_5_out), .in1(ALUR), .out(RAM_Wdata), .sel(EspCasePush));  // open: en
  Multiplexer #(.width(32)) multiplexer_9 (
    .in0({32{1'b1}}), .in1(KB_DATA_t), .out(multiplexer_9_out), .sel(KB_AVAIL));  // open: en
  Comparator #(.width(5)) comparator_1 (.a(WR), .b({5{1'b1}}), .eq(wr_sp));  // open: gt, lt
  Comparator #(.width(6)) comparator_2 (.a({o5, o4, o3, o2, o1, o0}), .b(6'b111000), .eq(IsPopOrPush));  // open: gt, lt
  Comparator #(.width(6)) comparator_3 (
    .a({b5_prime, b4_prime, b3_prime, b2_prime, b1_prime, b0_prime}), .b({6{1'b0}}), .eq(comparator_3_eq));  // open: gt, lt
  Multiplexer #(.select(2), .width(32)) multiplexer_10 (
    .in0(ALUR), .in1(RAM_Rdata), .in2(Hi), .in3(Lo), .out(multiplexer_10_out), .sel({WDS1, WDS0}));  // open: en
  Multiplexer #(.width(32)) multiplexer_11 (
    .in0(multiplexer_9_out), .in1(RAND), .out(multiplexer_11_out), .sel(and_2_out));  // open: en
  and and_2 (and_2_out, b1_prime, not_2_out);
  not not_2 (not_2_out, b0_prime);
  and and_3 (IsPoP, IsPopOrPush, comparator_3_eq);
  Comparator #(.width(6)) comparator_4 (
    .a({b5_prime, b4_prime, b3_prime, b2_prime, b1_prime, b0_prime}), .b(6'b000001), .eq(comparator_4_eq));  // open: gt, lt
  // Probe on WD
  Multiplexer #(.width(32)) multiplexer_12 (
    .in0(multiplexer_10_out), .in1(multiplexer_11_out), .out(WD), .sel(and_4_out));  // open: en
  and and_4 (and_4_out, I_Type[0], I_Type[1]);
  BranchControl branchcontrol_1 (
    .ZF(ZF), .Sconst(Const), .CLK(CLK), .LPC(LPC), .RSTPC(RSTPC), .PC(PC), .NF(NF), .TARGET(Target),
    .RegData({RA, TTY_DATA}), .Nop(nop), .BCode(B_CODE), .OP_CODE({o5, o4, o3, o2, o1, o0}),
    .FUNC_CODE({b5_prime, b4_prime, b3_prime, b2_prime, b1_prime, b0_prime}));
  and and_5 (IsPush, IsPopOrPush, comparator_4_eq);
  and and_6 (EspCase, wr_sp, LSP, IsPoP);
  and and_7 (EspCasePush, wr_sp, IsPush);
  RegisterFile registerfile_1 (
    .RR1(RS), .SP_Lo(LSP), .RR2(RT), .WR(WR), .SPIn(ALUR), .WD(WD), .SP(SP), .RW(RW), .DA({RA, TTY_DATA}),
    .Hi(Hi), .DB(RB), .Lo(Lo), .Clock(CLK), .Reset(RSTRF), .Hi_lo_L(LHi_Lo), .HiIn(HiIn), .LoIn(LoIn));
  ALU alu_1 (
    .op0(ALUI1), .op1(ALUI2), .Result(ALUR), .isZero(ZF), .isNegative(NF), .Lo(LoIn), .Hi(HiIn),
    .op_code(ALUOP), .MD_code({MS1, MS0}));

  // Other names for the same wires on the sheet: ALU2S[1:0] = {AS1, AS0};
  //   FUNC[5:0] = {b5_prime, b4_prime, b3_prime, b2_prime, b1_prime, b0_prime}; Hi_Lo_Lo = LHi_Lo; t0 = I_Type[0];
  //   WRS = I_Type[0]; t1 = I_Type[1]; Instruction[31:0] = instruct; MD_code[1:0] = {MS1, MS0};
  //   OP_CODE[5:0] = {o5, o4, o3, o2, o1, o0}; RA[6:0] = TTY_DATA; RST = RSTRF; SP_Lo = LSP; SPIn[31:0] = ALUR
endmodule

module BranchControl (
  input  ZF,
  input  NF,
  input  Nop,
  input  [2:0] BCode,
  input  [31:0] Sconst,
  input  [25:0] TARGET,
  input  [31:0] RegData,
  input  CLK,
  input  LPC,
  input  RSTPC,
  input  [5:0] OP_CODE,
  input  [5:0] FUNC_CODE,
  output [31:0] PC
);

  wire nor_1_out, not_1_out, or_1_out;
  wire [2:0] BS;
  wire [27:0] bit_extender_1_out, multiplier_2_out;
  wire [31:0] beq, bgtz, bit_extender_2_out, blez, bltz, bne, jump, offset_4, PC28_31ext, PC_4, PC_4_off_4,
       PC_prime, TAR_4;

  Register #(.width(32)) u_PC (.D(PC_prime), .en(LPC), .Q(PC), .clk(CLK), .clr(RSTPC));
  Adder #(.width(32)) adder_1 (.a(PC), .b(32'h4), .out(PC_4));  // open: cin, cout
  Multiplier #(.width(32)) multiplier_1 (.a(32'h4), .b(Sconst), .out(offset_4));  // open: cin, cout
  Adder #(.width(32)) adder_2 (.a(PC_4), .b(offset_4), .out(PC_4_off_4));  // open: cin, cout
  Multiplexer #(.width(32)) multiplexer_1 (.in0(PC_4), .in1(PC_4_off_4), .out(beq), .sel(ZF));  // open: en
  Multiplexer #(.width(32)) multiplexer_2 (.in0(PC_4), .in1(PC_4_off_4), .out(bne), .sel(not_1_out));  // open: en
  not not_1 (not_1_out, ZF);
  Multiplexer #(.width(32)) multiplexer_3 (.in0(PC_4), .in1(PC_4_off_4), .out(blez), .sel(or_1_out));  // open: en
  or or_1 (or_1_out, ZF, NF);
  Multiplexer #(.width(32)) multiplexer_4 (.in0(PC_4), .in1(PC_4_off_4), .out(bgtz), .sel(nor_1_out));  // open: en
  nor nor_1 (nor_1_out, NF, ZF);
  Multiplexer #(.width(32)) multiplexer_5 (.in0(PC_4), .in1(PC_4_off_4), .out(bltz), .sel(NF));  // open: en
  assign bit_extender_1_out = {{2{1'b0}}, TARGET};  // Bit_Extender bit_extender_1
  assign bit_extender_2_out = {{28{1'b0}}, PC[31:28]};  // Bit_Extender bit_extender_2
  Multiplier #(.width(28)) multiplier_2 (.a(28'h4), .b(bit_extender_1_out), .out(multiplier_2_out));  // open: cin, cout
  Multiplier #(.width(32)) multiplier_3 (
    .a(bit_extender_2_out), .b(32'h10000000), .out(PC28_31ext));  // open: cin, cout
  Adder #(.width(32)) adder_3 (.a(PC28_31ext), .b(TAR_4), .out(jump));  // open: cin, cout
  assign TAR_4 = {{4{1'b0}}, multiplier_2_out};  // Bit_Extender bit_extender_3
  BDecoder bdecoder_1 (.BCode(BCode), .FuncCode(FUNC_CODE), .OP_CODE(OP_CODE), .BSelector(BS));
  // Probe on BS
  Multiplexer #(.select(3), .width(32)) multiplexer_6 (
    .in0(PC_4), .in1(beq), .in2(bne), .in3(blez), .in4(bgtz), .in5(bltz), .in6(jump), .in7(RegData),
    .out(PC_prime), .sel(BS));  // open: en
  // Probe on PC_prime

  // Other names for the same wires on the sheet: offset[31:0] = Sconst; PC28_31[3:0] = PC[31:28]

  // Notes on the sheet:
  //   nop
  //   beq
  //   bne
  //   blez
  //   bgtz
  //   bltz
  //   jump
  //   BRANCH SELECTOR BS
  //   100-bgtz
  //   000-nop
  //   101-bltz
  //   001-beq
  //   110-j
  //   010-bne
  //   011-blez
  //   111-jr
endmodule

module BDecoder (
  input  [2:0] BCode,
  input  [5:0] FuncCode,
  input  [5:0] OP_CODE,
  output [2:0] BSelector
);

  wire and_1_out, and_3_out, and_4_out, and_5_out, and_6_out, and_7_out, IsBranch, JR, not_1_out, not_2_out,
       not_3_out, not_4_out, not_5_out, not_6_out, not_7_out, not_8_out, not_9_out, not_10_out, not_11_out,
       not_12_out, not_13_out;
  wire [1:0] I_TYPE;
  wire [2:0] multiplexer_1_out, multiplexer_2_out, or_3_out;

  nor nor_1 (IsBranch, OP_CODE[3], OP_CODE[4], OP_CODE[5]);
  not not_1 (not_1_out, FuncCode[5]);
  not not_2 (not_2_out, FuncCode[4]);
  not not_3 (not_3_out, FuncCode[2]);
  not not_4 (not_4_out, FuncCode[1]);
  not not_5 (not_5_out, FuncCode[0]);
  not not_6 (not_6_out, BCode[2]);
  and and_1 (and_1_out, BCode[1], BCode[0]);
  not not_7 (not_7_out, BCode[2]);
  not not_8 (not_8_out, BCode[0]);
  not not_9 (not_9_out, BCode[0]);
  not not_10 (not_10_out, BCode[1]);
  not not_11 (not_11_out, BCode[2]);
  not not_12 (not_12_out, BCode[1]);
  not not_13 (not_13_out, BCode[0]);
  and and_2 (JR, not_1_out, not_2_out, FuncCode[3], not_3_out, not_4_out, not_5_out);
  or or_1 (or_3_out[2], not_6_out, and_1_out);
  and and_3 (and_3_out, not_7_out, not_8_out);
  or or_2 (or_3_out[1], and_3_out, and_4_out, and_5_out);
  and and_4 (and_4_out, BCode[1], not_9_out);
  and and_5 (and_5_out, BCode[2], not_10_out, BCode[0]);
  and and_6 (and_6_out, not_11_out, not_12_out);
  or or_3 (or_3_out[0], and_6_out, and_7_out);
  and and_7 (and_7_out, BCode[2], not_13_out);
  I_TYPE i_type_1 (.OP_CODE(OP_CODE), .I_Type(I_TYPE));
  Multiplexer #(.width(3)) multiplexer_1 (
    .in0(3'b000), .in1(or_3_out), .out(multiplexer_1_out), .sel(IsBranch));  // open: en
  Multiplexer #(.width(3)) multiplexer_2 (.in0(3'b000), .in1(3'b111), .out(multiplexer_2_out), .sel(JR));  // open: en
  Multiplexer #(.select(2), .width(3)) multiplexer_3 (
    .in0(multiplexer_1_out), .in1(multiplexer_2_out), .in2(3'b110), .in3(3'b000), .out(BSelector),
    .sel(I_TYPE));  // open: en
  // Probe on I_TYPE

  // Other names for the same wires on the sheet: F0 = FuncCode[0]; F1 = FuncCode[1]; F2 = FuncCode[2];
  //   F3 = FuncCode[3]; F4 = FuncCode[4]; F5 = FuncCode[5]; b0 = OP_CODE[0]; OP[5:0] = OP_CODE; b1 = OP_CODE[1];
  //   b2 = OP_CODE[2]; b3 = OP_CODE[3]; b4 = OP_CODE[4]; b5 = OP_CODE[5]
endmodule

module ALUD (
  input  [5:0] FUNC_CODE,
  output [2:0] ALUOP
);

  wire A0, A1, A2, and_1_out, and_2_out, and_3_out, and_4_out, and_5_out, and_6_out, and_7_out, not_1_out,
       not_2_out, not_3_out, not_4_out, not_5_out, not_6_out;
  wire [1:0] bit_extender_1_out;

  and and_1 (and_1_out, FUNC_CODE[2], FUNC_CODE[1]);
  not not_1 (not_1_out, FUNC_CODE[1]);
  not not_2 (not_2_out, FUNC_CODE[2]);
  not not_3 (not_3_out, FUNC_CODE[1]);
  not not_4 (not_4_out, FUNC_CODE[3]);
  not not_5 (not_5_out, FUNC_CODE[2]);
  not not_6 (not_6_out, FUNC_CODE[1]);
  or or_1 (A2, and_1_out, FUNC_CODE[3]);
  and and_2 (and_2_out, FUNC_CODE[2], not_1_out);
  and and_3 (and_3_out, FUNC_CODE[3], FUNC_CODE[1]);
  and and_4 (and_4_out, not_2_out, FUNC_CODE[0]);
  and and_5 (and_5_out, not_3_out, FUNC_CODE[0]);
  and and_6 (and_6_out, not_4_out, not_5_out, FUNC_CODE[1]);
  and and_7 (and_7_out, FUNC_CODE[3], not_6_out);
  or or_2 (A1, and_2_out, and_3_out);
  or or_3 (A0, and_4_out, and_5_out, and_6_out, and_7_out);
  assign bit_extender_1_out = {{1{A1}}, A0};  // Bit_Extender bit_extender_1
  assign ALUOP = {{1{A2}}, bit_extender_1_out};  // Bit_Extender bit_extender_2

  // Other names for the same wires on the sheet: b0 = FUNC_CODE[0]; FC[5:0] = FUNC_CODE; b1 = FUNC_CODE[1];
  //   b2 = FUNC_CODE[2]; b3 = FUNC_CODE[3]
endmodule

module ALUDECODER (
  input  [5:0] OP_CODE,
  input  [5:0] FUNC_CODE,
  output [2:0] ALUOP
);

  wire [1:0] ALUOPTYPE;
  wire [2:0] ALUOPI, ALUOPR;

  ALUD alud_1 (.FUNC_CODE(FUNC_CODE), .ALUOP(ALUOPR));
  ALUDecI aludeci_1 (.OP_CODE(OP_CODE), .ALUOPI(ALUOPI));
  I_TYPE i_type_1 (.OP_CODE(OP_CODE), .I_Type(ALUOPTYPE));
  // Probe on ALUOPTYPE
  Multiplexer #(.select(2), .width(3)) multiplexer_1 (
    .in0(ALUOPI), .in1(ALUOPR), .in2(3'b000), .in3(3'b000), .out(ALUOP), .sel(ALUOPTYPE));  // open: en

  // Other names for the same wires on the sheet: FC[5:0] = FUNC_CODE; OP[5:0] = OP_CODE
endmodule

module ControlUnit_2 (
  input  [31:0] Instruction,
  input  on,
  output RW,
  output LPC,
  output SP_LO,
  output HI_LO,
  output A1S1,
  output A1S0,
  output A2S1,
  output A2S0,
  output WDS1,
  output WDS0,
  output RAR,
  output RAW,
  output Ms1,
  output Ms0,
  output TTY_EN,
  output Halt,
  output KBD_EN,
  output [2:0] ALUOP
);

  wire Nop;
  wire [1:0] ISelector;
  wire [5:0] FunCode, OpCode;
  wire [16:0] itypecontrol_1_rw, multiplexer_1_out, n4typecontrol_1_reglo, rtypecontrol_1_rw;

  I_TYPE i_type_1 (.OP_CODE(OpCode), .I_Type(ISelector));
  ALUDECODER aludecoder_1 (.OP_CODE(OpCode), .FUNC_CODE(FunCode), .ALUOP(ALUOP));
  Spliter spliter_1 (
    .in_1(Instruction), .opcode(OpCode), .funccode(FunCode), .Nop(Nop));  // open: B_Code, rs, rt, rd, Unsigned, Signed, target
  ItypeControl itypecontrol_1 (
    .On(on), .OpCode(OpCode), .RW(itypecontrol_1_rw[0]), .LPC(itypecontrol_1_rw[1]),
    .SP_LO(itypecontrol_1_rw[2]), .HI_LO(itypecontrol_1_rw[3]), .A1S1(itypecontrol_1_rw[4]),
    .A1S0(itypecontrol_1_rw[5]), .A2S1(itypecontrol_1_rw[6]), .A2S0(itypecontrol_1_rw[7]),
    .WDS1(itypecontrol_1_rw[8]), .WDS0(itypecontrol_1_rw[9]), .RAR(itypecontrol_1_rw[10]),
    .RAW(itypecontrol_1_rw[11]), .Ms1(itypecontrol_1_rw[12]), .Ms0(itypecontrol_1_rw[13]),
    .TTY_EN(itypecontrol_1_rw[14]), .Halt(itypecontrol_1_rw[15]), .KBD_EN(itypecontrol_1_rw[16]));
  RtypeControl rtypecontrol_1 (
    .On(on), .nop(Nop), .FuncCode(FunCode), .RW(rtypecontrol_1_rw[0]), .LPC(rtypecontrol_1_rw[1]),
    .SP_LO(rtypecontrol_1_rw[2]), .HI_LO(rtypecontrol_1_rw[3]), .A1S1(rtypecontrol_1_rw[4]),
    .A1S0(rtypecontrol_1_rw[5]), .A2S1(rtypecontrol_1_rw[6]), .A2S0(rtypecontrol_1_rw[7]),
    .WDS1(rtypecontrol_1_rw[8]), .WDS0(rtypecontrol_1_rw[9]), .RaR(rtypecontrol_1_rw[10]),
    .RaW(rtypecontrol_1_rw[11]), .Ms1(rtypecontrol_1_rw[12]), .Ms0(rtypecontrol_1_rw[13]),
    .TTY_EN(rtypecontrol_1_rw[14]), .Halt(rtypecontrol_1_rw[15]), .KBD_EN(rtypecontrol_1_rw[16]));
  Multiplexer #(.width(17)) multiplexer_1 (
    .in0({17{1'b0}}), .in1(17'h2), .out(multiplexer_1_out), .sel(on));  // open: en
  _4TypeControl u_4typecontrol_1 (
    .FuncCode(FunCode), .On(on), .SP_LO(n4typecontrol_1_reglo[2]), .TTY_EN(n4typecontrol_1_reglo[14]),
    .HI_LO(n4typecontrol_1_reglo[3]), .RegLo(n4typecontrol_1_reglo[0]), .A1S1(n4typecontrol_1_reglo[4]),
    .Halt(n4typecontrol_1_reglo[15]), .A1S0(n4typecontrol_1_reglo[5]), .A2S1(n4typecontrol_1_reglo[6]),
    .LPC(n4typecontrol_1_reglo[1]), .A2S0(n4typecontrol_1_reglo[7]), .WDS1(n4typecontrol_1_reglo[8]),
    .KBD_EN(n4typecontrol_1_reglo[16]), .WDS0(n4typecontrol_1_reglo[9]), .RAR(n4typecontrol_1_reglo[10]),
    .RAW(n4typecontrol_1_reglo[11]), .Ms1(n4typecontrol_1_reglo[12]), .Ms0(n4typecontrol_1_reglo[13]));
  Multiplexer #(.select(2), .width(17)) multiplexer_2 (
    .in0(itypecontrol_1_rw), .in1(rtypecontrol_1_rw), .in2(multiplexer_1_out), .in3(n4typecontrol_1_reglo),
    .out({KBD_EN, Halt, TTY_EN, Ms0, Ms1, RAW, RAR, WDS0, WDS1, A2S0, A2S1, A1S0, A1S1, HI_LO, SP_LO, LPC, RW}),
    .sel(ISelector));  // open: en
endmodule

module I_TYPE (
  input  [5:0] OP_CODE,
  output [1:0] I_Type
);

  wire and_1_out, and_2_out, and_3_out, and_4_out, nor_1_out, not_1_out, not_2_out, not_3_out, not_4_out, T0,
       T1;

  not not_1 (not_1_out, OP_CODE[1]);
  not not_2 (not_2_out, OP_CODE[1]);
  nor nor_1 (nor_1_out, OP_CODE[5], OP_CODE[4], OP_CODE[3], OP_CODE[2], OP_CODE[1], OP_CODE[0]);
  and and_1 (and_1_out, OP_CODE[5], OP_CODE[4], OP_CODE[3], not_3_out, not_1_out, not_4_out);
  not not_3 (not_3_out, OP_CODE[2]);
  not not_4 (not_4_out, OP_CODE[0]);
  and and_2 (and_2_out, OP_CODE[5], OP_CODE[4], OP_CODE[3], OP_CODE[2], OP_CODE[1], OP_CODE[0]);
  and and_3 (and_3_out, OP_CODE[5], OP_CODE[4], OP_CODE[3], OP_CODE[2], not_2_out, OP_CODE[0]);
  and and_4 (and_4_out, OP_CODE[5], OP_CODE[4], OP_CODE[3], OP_CODE[2], OP_CODE[1], OP_CODE[0]);
  or or_1 (T0, nor_1_out, and_1_out, and_2_out);
  or or_2 (T1, and_3_out, and_4_out);
  assign I_Type = {{1{T1}}, T0};  // Bit_Extender bit_extender_1

  // Other names for the same wires on the sheet: b0 = OP_CODE[0]; OP[5:0] = OP_CODE; b1 = OP_CODE[1]; b2 = OP_CODE[2];
  //   b3 = OP_CODE[3]; b4 = OP_CODE[4]; b5 = OP_CODE[5]

  // Notes on the sheet:
  //   00-I-TYPE
  //   01-R-TYPE
  //   10-J-TYPE
  //   11-111111 instruct
endmodule

module RtypeControl (
  input  On,
  input  nop,
  input  [5:0] FuncCode,
  output RW,
  output LPC,
  output SP_LO,
  output HI_LO,
  output A1S1,
  output A1S0,
  output A2S1,
  output A2S0,
  output WDS1,
  output WDS0,
  output RaR,
  output RaW,
  output Ms1,
  output Ms0,
  output TTY_EN,
  output Halt,
  output KBD_EN
);

  wire and_1_out, and_2_out, and_8_out, and_9_out, not_1_out, not_2_out, not_3_out, not_4_out, not_5_out,
       not_6_out, not_7_out, not_8_out, not_9_out, not_10_out, not_11_out, not_12_out, not_13_out,
       not_14_out, not_15_out, not_16_out, not_17_out, not_18_out, not_19_out, not_20_out, not_21_out;

  not not_1 (not_1_out, nop);
  not not_2 (not_2_out, FuncCode[3]);
  not not_3 (not_3_out, FuncCode[0]);
  not not_4 (not_4_out, nop);
  not not_5 (not_5_out, FuncCode[5]);
  not not_6 (not_6_out, FuncCode[4]);
  not not_7 (not_7_out, FuncCode[3]);
  not not_8 (not_8_out, FuncCode[5]);
  not not_9 (not_9_out, FuncCode[3]);
  not not_10 (not_10_out, FuncCode[5]);
  not not_11 (not_11_out, FuncCode[3]);
  not not_12 (not_12_out, FuncCode[5]);
  not not_13 (not_13_out, FuncCode[4]);
  not not_14 (not_14_out, FuncCode[5]);
  not not_15 (not_15_out, nop);
  not not_16 (not_16_out, FuncCode[5]);
  not not_17 (not_17_out, FuncCode[4]);
  not not_18 (not_18_out, FuncCode[3]);
  not not_19 (not_19_out, FuncCode[0]);
  not not_20 (not_20_out, FuncCode[3]);
  not not_21 (not_21_out, FuncCode[2]);
  and and_1 (and_1_out, On, not_1_out, not_2_out, not_3_out);
  and and_2 (and_2_out, On, FuncCode[5]);
  and and_3 (SP_LO, On, not_4_out, not_5_out, not_6_out, not_7_out);
  and and_4 (HI_LO, On, FuncCode[4], FuncCode[3]);
  and and_5 (A1S0, On, not_8_out, not_9_out);
  and and_6 (A2S1, On, not_10_out, not_11_out);
  and and_7 (WDS1, On, FuncCode[4]);
  and and_8 (and_8_out, On, not_12_out, not_13_out);
  and and_9 (and_9_out, On, not_14_out, FuncCode[1]);
  and and_10 (RaW, On, not_20_out, not_21_out, FuncCode[0]);
  and and_11 (Ms1, On, FuncCode[1]);
  and and_12 (Ms0, On, FuncCode[0]);
  or or_1 (RW, and_1_out, and_2_out);
  or or_2 (WDS0, and_8_out, and_9_out);
  and and_13 (RaR, On, not_15_out, not_16_out, not_17_out, not_18_out, not_19_out);

  assign A1S1 = 1'b0;
  assign A2S0 = 1'b0;
  assign Halt = 1'b0;
  assign KBD_EN = 1'b0;
  assign LPC = On;
  assign TTY_EN = 1'b0;

  // Other names for the same wires on the sheet: F0 = FuncCode[0]; F1 = FuncCode[1]; F2 = FuncCode[2];
  //   F3 = FuncCode[3]; F4 = FuncCode[4]; F5 = FuncCode[5]
endmodule

module ItypeControl (
  input  On,
  input  [5:0] OpCode,
  output RW,
  output LPC,
  output SP_LO,
  output HI_LO,
  output A1S1,
  output A1S0,
  output A2S1,
  output A2S0,
  output WDS1,
  output WDS0,
  output RAR,
  output RAW,
  output Ms1,
  output Ms0,
  output TTY_EN,
  output Halt,
  output KBD_EN
);

  wire and_1_out, and_2_out, and_3_out, and_4_out, and_5_out, and_6_out, and_7_out, not_1_out, not_2_out,
       not_3_out, not_4_out, not_5_out, not_6_out, not_7_out, not_8_out, not_9_out, not_10_out;

  not not_1 (not_1_out, OpCode[5]);
  not not_2 (not_2_out, OpCode[3]);
  not not_3 (not_3_out, OpCode[3]);
  not not_4 (not_4_out, OpCode[2]);
  not not_5 (not_5_out, OpCode[1]);
  not not_6 (not_6_out, OpCode[5]);
  not not_7 (not_7_out, OpCode[3]);
  not not_8 (not_8_out, OpCode[2]);
  not not_9 (not_9_out, OpCode[3]);
  not not_10 (not_10_out, OpCode[3]);
  and and_1 (and_1_out, On, not_1_out, OpCode[3]);
  and and_2 (and_2_out, On, OpCode[5], not_2_out);
  and and_3 (and_3_out, On, not_3_out, not_4_out, not_5_out);
  and and_4 (and_4_out, On, not_6_out, not_7_out, OpCode[1]);
  and and_5 (and_5_out, On, not_8_out);
  and and_6 (and_6_out, On, OpCode[1]);
  and and_7 (and_7_out, On, OpCode[3]);
  and and_8 (WDS0, On, not_9_out);
  and and_9 (RAR, On, OpCode[5], not_10_out);
  and and_10 (RAW, On, OpCode[5], OpCode[3]);
  or or_1 (RW, and_1_out, and_2_out);
  or or_2 (A2S1, and_3_out, and_4_out);
  or or_3 (A2S0, and_5_out, and_6_out, and_7_out);

  assign A1S0 = 1'b0;
  assign A1S1 = 1'b0;
  assign Halt = 1'b0;
  assign HI_LO = 1'b0;
  assign KBD_EN = 1'b0;
  assign LPC = On;
  assign Ms0 = 1'b0;
  assign Ms1 = 1'b0;
  assign SP_LO = 1'b0;
  assign TTY_EN = 1'b0;
  assign WDS1 = 1'b0;

  // Other names for the same wires on the sheet: Op1 = OpCode[1]; Op2 = OpCode[2]; Op3 = OpCode[3]; Op5 = OpCode[5]
endmodule

module _4TypeControl (
  input  [5:0] FuncCode,
  input  On,
  output SP_LO,
  output TTY_EN,
  output HI_LO,
  output RegLo,
  output A1S1,
  output Halt,
  output A1S0,
  output A2S1,
  output LPC,
  output A2S0,
  output WDS1,
  output KBD_EN,
  output WDS0,
  output RAR,
  output RAW,
  output Ms1,
  output Ms0
);

  wire and_4_out, and_5_out, not_1_out, not_2_out, not_3_out, not_4_out;

  not not_1 (not_1_out, FuncCode[1]);
  not not_2 (not_2_out, FuncCode[0]);
  and and_1 (Halt, On, FuncCode[1], FuncCode[0]);
  not not_3 (not_3_out, FuncCode[1]);
  not not_4 (not_4_out, FuncCode[0]);
  and and_2 (TTY_EN, On, not_1_out, FuncCode[0]);
  and and_3 (RegLo, On, not_2_out);
  and and_4 (and_4_out, On, not_3_out);
  and and_5 (and_5_out, On, not_4_out);
  and and_6 (KBD_EN, ~FuncCode[1], ~FuncCode[0], On);  // AND_Gate
  or or_1 (LPC, and_4_out, and_5_out);

  assign A1S0 = 1'b0;
  assign A1S1 = 1'b0;
  assign A2S0 = 1'b0;
  assign A2S1 = 1'b0;
  assign HI_LO = 1'b0;
  assign Ms0 = 1'b0;
  assign Ms1 = 1'b0;
  assign RAR = 1'b0;
  assign RAW = 1'b0;
  assign SP_LO = 1'b0;
  assign WDS0 = 1'b0;
  assign WDS1 = 1'b0;

  // Other names for the same wires on the sheet: F0 = FuncCode[0]; F1 = FuncCode[1]; F2 = FuncCode[2];
  //   F3 = FuncCode[3]; F4 = FuncCode[4]; F5 = FuncCode[5]
endmodule

module Cache_2 (
  input  [31:0] Adress,
  input  Clock,
  input  RESET,
  input  [31:0] MemoryData0,
  input  [31:0] MemoryData1,
  input  [31:0] MemoryData2,
  input  [31:0] MemoryData3,
  input  RW,
  input  Valided,
  input  [31:0] DataWrite,
  input  RamWrite,
  output HIT,
  output [31:0] SetData,
  output isValid
);

  wire comparator_1_eq, isV0, isV1, isV2, isV3, isV4, isV5, isV6, isV7, SL0, SL1, SL2, SL3, SL4, SL5, SL6,
       SL7, SwL0, SwL1, SwL2, SwL3, SwL4, SwL5, SwL6, SwL7, V0, V1, V2, V3, V4, V5, V6, V7;
  wire [24:0] multiplexer_1_out, T0, T1, T2, T3, T4, T5, T6, T7;
  wire [31:0] S0, S1, S2, S3, S4, S5, S6, S7;

  CacheSet u_S0 (
    .Tag(Adress[31:7]), .BlockSelect(Adress[3:2]), .Clock(Clock), .Reset(RESET), .Load(SL0), .Loadw(SwL0),
    .Dataw(DataWrite), .Data0(MemoryData0), .Data1(MemoryData1), .Data2(MemoryData2), .Data3(MemoryData3),
    .Valided(V0), .CanWrite(HIT), .DataOut(S0), .DataOut_2(T0), .isValid(isV0));
  CacheSet u_S4 (
    .Tag(Adress[31:7]), .BlockSelect(Adress[3:2]), .Clock(Clock), .Reset(RESET), .Load(SL4), .Loadw(SwL4),
    .Dataw(DataWrite), .Data0(MemoryData0), .Data1(MemoryData1), .Data2(MemoryData2), .Data3(MemoryData3),
    .Valided(V4), .CanWrite(HIT), .DataOut(S4), .DataOut_2(T4), .isValid(isV4));
  Multiplexer #(.select(3), .width(25)) multiplexer_1 (
    .in0(T0), .in1(T1), .in2(T2), .in3(T3), .in4(T4), .in5(T5), .in6(T6), .in7(T7), .out(multiplexer_1_out),
    .sel(Adress[6:4]));  // open: en
  Multiplexer #(.select(3), .width(32)) multiplexer_2 (
    .in0(S0), .in1(S1), .in2(S2), .in3(S3), .in4(S4), .in5(S5), .in6(S6), .in7(S7), .out(SetData),
    .sel(Adress[6:4]));  // open: en
  Multiplexer #(.select(3)) multiplexer_3 (
    .in0(isV0), .in1(isV1), .in2(isV2), .in3(isV3), .in4(isV4), .in5(isV5), .in6(isV6), .in7(isV7),
    .out(isValid), .sel(Adress[6:4]));  // open: en
  Comparator #(.width(25)) comparator_1 (
    .a(multiplexer_1_out), .b(Adress[31:7]), .eq(comparator_1_eq));  // open: gt, lt
  and and_1 (HIT, comparator_1_eq, isValid);
  CacheSet u_S1 (
    .Tag(Adress[31:7]), .BlockSelect(Adress[3:2]), .Clock(Clock), .Reset(RESET), .Load(SL1), .Loadw(SwL1),
    .Dataw(DataWrite), .Data0(MemoryData0), .Data1(MemoryData1), .Data2(MemoryData2), .Data3(MemoryData3),
    .Valided(V1), .CanWrite(HIT), .DataOut(S1), .DataOut_2(T1), .isValid(isV1));
  CacheSet u_S5 (
    .Tag(Adress[31:7]), .BlockSelect(Adress[3:2]), .Clock(Clock), .Reset(RESET), .Load(SL5), .Loadw(SwL5),
    .Dataw(DataWrite), .Data0(MemoryData0), .Data1(MemoryData1), .Data2(MemoryData2), .Data3(MemoryData3),
    .Valided(V5), .CanWrite(HIT), .DataOut(S5), .DataOut_2(T5), .isValid(isV5));
  Demultiplexer #(.select(3)) demultiplexer_1 (
    .out0(SL0), .out1(SL1), .out2(SL2), .out3(SL3), .out4(SL4), .out5(SL5), .out6(SL6), .out7(SL7), .in(RW),
    .sel(Adress[6:4]));  // open: en
  Demultiplexer #(.select(3)) demultiplexer_2 (
    .out0(V0), .out1(V1), .out2(V2), .out3(V3), .out4(V4), .out5(V5), .out6(V6), .out7(V7), .in(Valided),
    .sel(Adress[6:4]));  // open: en
  Demultiplexer #(.select(3)) demultiplexer_3 (
    .out0(SwL0), .out1(SwL1), .out2(SwL2), .out3(SwL3), .out4(SwL4), .out5(SwL5), .out6(SwL6), .out7(SwL7),
    .in(RamWrite), .sel(Adress[6:4]));  // open: en
  CacheSet u_S2 (
    .Tag(Adress[31:7]), .BlockSelect(Adress[3:2]), .Clock(Clock), .Reset(RESET), .Load(SL2), .Loadw(SwL2),
    .Dataw(DataWrite), .Data0(MemoryData0), .Data1(MemoryData1), .Data2(MemoryData2), .Data3(MemoryData3),
    .Valided(V2), .CanWrite(HIT), .DataOut(S2), .DataOut_2(T2), .isValid(isV2));
  CacheSet u_S6 (
    .Tag(Adress[31:7]), .BlockSelect(Adress[3:2]), .Clock(Clock), .Reset(RESET), .Load(SL6), .Loadw(SwL6),
    .Dataw(DataWrite), .Data0(MemoryData0), .Data1(MemoryData1), .Data2(MemoryData2), .Data3(MemoryData3),
    .Valided(V6), .CanWrite(HIT), .DataOut(S6), .DataOut_2(T6), .isValid(isV6));
  CacheSet u_S3 (
    .Tag(Adress[31:7]), .BlockSelect(Adress[3:2]), .Clock(Clock), .Reset(RESET), .Load(SL3), .Loadw(SwL3),
    .Dataw(DataWrite), .Data0(MemoryData0), .Data1(MemoryData1), .Data2(MemoryData2), .Data3(MemoryData3),
    .Valided(V3), .CanWrite(HIT), .DataOut(S3), .DataOut_2(T3), .isValid(isV3));
  CacheSet u_S7 (
    .Tag(Adress[31:7]), .BlockSelect(Adress[3:2]), .Clock(Clock), .Reset(RESET), .Load(SL7), .Loadw(SwL7),
    .Dataw(DataWrite), .Data0(MemoryData0), .Data1(MemoryData1), .Data2(MemoryData2), .Data3(MemoryData3),
    .Valided(V7), .CanWrite(HIT), .DataOut(S7), .DataOut_2(T7), .isValid(isV7));

  // Other names for the same wires on the sheet: ABlock[1:0] = Adress[3:2]; ASet[2:0] = Adress[6:4];
  //   ATag[24:0] = Adress[31:7]; Data0[31:0] = MemoryData0; Data1[31:0] = MemoryData1; Data2[31:0] = MemoryData2;
  //   Data3[31:0] = MemoryData3; R_W = RW; SD[31:0] = SetData
endmodule

module CacheSet (
  input  [24:0] Tag,
  input  [1:0] BlockSelect,
  input  Clock,
  input  Reset,
  input  Load,
  input  Loadw,
  input  [31:0] Dataw,
  input  [31:0] Data0,
  input  [31:0] Data1,
  input  [31:0] Data2,
  input  [31:0] Data3,
  input  Valided,
  input  CanWrite,
  output [31:0] DataOut,
  output [24:0] DataOut_2,
  output isValid
);

  wire and_1_out, and_2_out, and_3_out, and_4_out, Load0, Load1, Load2, Load3;
  wire [31:0] B0, B1, B2, B3, Data0_t, Data1_t, Data2_t, Data3_t, ram_translate_1_translated,
       ram_translate_2_translated, ram_translate_3_translated, ram_translate_4_translated,
       ram_translate_5_translated;

  RAM_TRANSLATE ram_translate_1 (.RAM_IN(Dataw), .TRANSLATED(ram_translate_1_translated));
  Register #(.width(25)) u_Tag (.D(Tag), .en(Load), .Q(DataOut_2), .clk(Clock), .clr(Reset));
  Multiplexer #(.select(2), .width(32)) multiplexer_1 (
    .in0(B0), .in1(B1), .in2(B2), .in3(B3), .out(DataOut), .sel(BlockSelect));  // open: en
  D_Flip_Flop #(.trigger("falling")) d_ff_1 (
    .clk(Clock), .D(Valided), .Q(isValid), .en(Valided), .reset(Reset));  // open: Qn, preset
  and and_1 (and_1_out, Loadw, ~BlockSelect[0], ~BlockSelect[1], CanWrite);  // AND_Gate
  and and_2 (and_2_out, Loadw, BlockSelect[0], ~BlockSelect[1], CanWrite);  // AND_Gate
  and and_3 (and_3_out, Loadw, ~BlockSelect[0], BlockSelect[1], CanWrite);  // AND_Gate
  and and_4 (and_4_out, Loadw, BlockSelect[0], BlockSelect[1], CanWrite);
  or or_1 (Load0, Load, and_1_out);
  or or_2 (Load1, Load, and_2_out);
  or or_3 (Load2, Load, and_3_out);
  or or_4 (Load3, Load, and_4_out);
  Register #(.width(32)) u_B0 (.D(Data0_t), .en(Load0), .Q(B0), .clk(Clock), .clr(Reset));
  Register #(.width(32)) u_B1 (.D(Data1_t), .en(Load1), .Q(B1), .clk(Clock), .clr(Reset));
  RAM_TRANSLATE ram_translate_2 (.RAM_IN(B0), .TRANSLATED(ram_translate_2_translated));
  RAM_TRANSLATE ram_translate_3 (.RAM_IN(B1), .TRANSLATED(ram_translate_3_translated));
  Register #(.width(32)) u_B2 (.D(Data2_t), .en(Load2), .Q(B2), .clk(Clock), .clr(Reset));
  Register #(.width(32)) u_B3 (.D(Data3_t), .en(Load3), .Q(B3), .clk(Clock), .clr(Reset));
  Multiplexer #(.width(32)) multiplexer_2 (.in0(Data0), .in1(Dataw), .out(Data0_t), .sel(Loadw));  // open: en
  Multiplexer #(.width(32)) multiplexer_3 (.in0(Data1), .in1(Dataw), .out(Data1_t), .sel(Loadw));  // open: en
  RAM_TRANSLATE ram_translate_4 (.RAM_IN(B2), .TRANSLATED(ram_translate_4_translated));
  RAM_TRANSLATE ram_translate_5 (.RAM_IN(B3), .TRANSLATED(ram_translate_5_translated));
  Multiplexer #(.width(32)) multiplexer_4 (.in0(Data2), .in1(Dataw), .out(Data2_t), .sel(Loadw));  // open: en
  Multiplexer #(.width(32)) multiplexer_5 (.in0(Data3), .in1(Dataw), .out(Data3_t), .sel(Loadw));  // open: en

  // Other names for the same wires on the sheet: ATag[24:0] = Tag; BS[1:0] = BlockSelect; BS0 = BlockSelect[0];
  //   BS1 = BlockSelect[1]; Data0in[31:0] = Data0; Data1in[31:0] = Data1; Data2in[31:0] = Data2;
  //   Data3in[31:0] = Data3; Tag_t[24:0] = DataOut_2
endmodule

module ALUDecI (
  input  [5:0] OP_CODE,
  output [2:0] ALUOPI
);

  wire A0, A1, A2, and_2_out, and_3_out, and_4_out, and_5_out, and_6_out, not_1_out, not_2_out, not_3_out,
       not_4_out, not_5_out, not_6_out, not_7_out;
  wire [1:0] bit_extender_1_out;

  not not_1 (not_1_out, OP_CODE[5]);
  and and_1 (A2, not_1_out, OP_CODE[3], OP_CODE[1]);
  not not_2 (not_2_out, OP_CODE[5]);
  not not_3 (not_3_out, OP_CODE[2]);
  and and_2 (and_2_out, not_2_out, not_3_out, OP_CODE[1]);
  and and_3 (and_3_out, OP_CODE[3], OP_CODE[2], not_4_out);
  not not_4 (not_4_out, OP_CODE[1]);
  not not_5 (not_5_out, OP_CODE[3]);
  and and_4 (and_4_out, not_5_out, not_6_out);
  not not_6 (not_6_out, OP_CODE[1]);
  not not_7 (not_7_out, OP_CODE[5]);
  and and_5 (and_5_out, not_7_out, OP_CODE[0]);
  and and_6 (and_6_out, OP_CODE[2], OP_CODE[1]);
  or or_1 (A1, and_2_out, and_3_out);
  or or_2 (A0, and_4_out, and_5_out, and_6_out);
  assign bit_extender_1_out = {{1{A1}}, A0};  // Bit_Extender bit_extender_1
  assign ALUOPI = {{1{A2}}, bit_extender_1_out};  // Bit_Extender bit_extender_2

  // Other names for the same wires on the sheet: b0 = OP_CODE[0]; OP[5:0] = OP_CODE; b1 = OP_CODE[1]; b2 = OP_CODE[2];
  //   b3 = OP_CODE[3]; b5 = OP_CODE[5]
endmodule

module RAMUI (
  input  HIT,
  input  RamRead,
  input  WriteRam,
  input  CLk,
  input  LoPCin,
  input  LoRegin,
  input  LoSP,
  input  [3:0] RRT,
  input  [3:0] WRT,
  input  RST,
  input  HitInsCache,
  input  isValid,
  input  isValidInst,
  input  [31:0] PC,
  input  ON,
  input  RST_2,
  output LoadCache,
  output LoadInstCache,
  output RamAddS,
  output RamUse,
  output RamWrite,
  output LValid,
  output LValidInst,
  output CacheWrite,
  output LoPC,
  output LoReg,
  output LoSP_2
);

  wire and_6_out, C_0, C_1, CInc, CInc1, CInc2, demultiplexer_1_out0, demultiplexer_1_out1,
       demultiplexer_3_out1, HIT_t, HitInsCache_t, INIT, LoadCond, LoadCond2, LoadCond4, LoadCondNR,
       LoadCondRead, LoadCondRead_prime, not_1_out, or_1_out, or_5_out, or_11_out, or_13_out, or_14_out,
       PC_0, RamAddS2, Recharge, Recharged, RechargeRST, RorW, RR_prime, RSTLoadConRead, RSTLoadConRead2,
       WHILE_2_q, WHILE_3_q, WHILE_q;
  wire [3:0] Count, InC;

  Comparator #(.width(32)) comparator_1 (.a(PC), .b({32{1'b0}}), .eq(PC_0));  // open: gt, lt
  or or_1 (or_1_out, INIT, LoadCond4, LoadCond2, LoadCache, LoadInstCache);
  or or_2 (RamAddS, RamWrite, LoadCache, RamAddS2);
  and and_1 (LoPC, LoPCin, LoadCond);
  and and_2 (LoReg, LoRegin, LoadCond);
  and and_3 (LoSP_2, LoSP, LoadCond);
  and and_4 (HIT_t, HIT, isValid);
  and and_5 (HitInsCache_t, HitInsCache, isValidInst);
  Demultiplexer demultiplexer_1 (
    .out0(demultiplexer_1_out0), .out1(demultiplexer_1_out1), .in(RechargeRST), .sel(RorW));  // open: en
  D_Flip_Flop IDLE (.clk(CLk), .D(or_1_out), .Q(RechargeRST), .preset(RST));  // open: Qn, en, reset
  or or_3 (RR_prime, RSTLoadConRead2, Recharge, CInc);
  Demultiplexer demultiplexer_2 (
    .out0(RSTLoadConRead2), .out1(LoadCond4), .in(demultiplexer_1_out0), .sel(HitInsCache_t));  // open: en
  Demultiplexer demultiplexer_3 (
    .out0(CacheWrite), .out1(demultiplexer_3_out1), .in(demultiplexer_1_out1), .sel(RamRead));  // open: en
  D_Flip_Flop WHILE (.clk(CLk), .D(RR_prime), .Q(WHILE_q), .reset(RST));  // open: Qn, preset, en
  Demultiplexer demultiplexer_4 (.out0(CInc), .out1(LoadInstCache), .in(WHILE_q), .sel(C_0));  // open: en
  or or_4 (RamWrite, CacheWrite, CInc1);
  Demultiplexer demultiplexer_5 (
    .out0(RSTLoadConRead), .out1(LoadCond2), .in(demultiplexer_3_out1), .sel(HIT_t));  // open: en
  Multiplexer #(.width(4)) multiplexer_1 (.in0(WRT), .in1(RRT), .out(InC), .sel(or_5_out));  // open: en
  or or_5 (or_5_out, RamRead, RR_prime);
  and and_6 (and_6_out, Recharged, LoadInstCache);
  D_Flip_Flop WHILE_2 (.clk(CLk), .D(RamWrite), .Q(WHILE_2_q), .reset(RST));  // open: Qn, preset, en
  or or_6 (RamAddS2, RSTLoadConRead, CInc2);
  // Probe on InC
  or or_7 (RorW, WriteRam, RamRead);
  Comparator #(.width(4), .mode("unsigned")) comparator_2 (.a(Count), .b(4'b0000), .eq(C_0));  // open: gt, lt
  Comparator #(.width(4), .mode("unsigned")) comparator_3 (.a(Count), .b(4'b0001), .eq(C_1));  // open: gt, lt
  or or_8 (LoadCondNR, and_6_out, LoadCond2, LoadCond4);
  or or_9 (LoadCondRead, LoadCache, LoadInstCache);
  or or_10 (RamUse, RamAddS2, RamWrite, CInc, LoadInstCache, LoadCache);
  Demultiplexer demultiplexer_6 (.out0(CInc1), .out1(Recharge), .in(WHILE_2_q), .sel(C_0));  // open: en
  D_Flip_Flop WHILE_3 (.clk(CLk), .D(RamAddS2), .Q(WHILE_3_q), .reset(RST));  // open: Qn, preset, en
  Demultiplexer demultiplexer_7 (.out0(CInc2), .out1(LoadCache), .in(WHILE_3_q), .sel(C_0));  // open: en
  or or_11 (or_11_out, CInc, CInc1, CInc2);
  or or_12 (LoadCond, LoadCondNR, LoadCondRead_prime);
  not not_1 (not_1_out, RamUse);
  D_Flip_Flop d_ff_1 (.clk(CLk), .D(Recharge), .Q(Recharged), .en(Recharge), .reset(or_13_out));  // open: Qn, preset
  or or_13 (or_13_out, RST, RechargeRST);
  Counter #(.width(4), .max('hf)) c (
    .load(1'b1), .D(InC), .count(or_11_out), .Q(Count), .clk(CLk), .clr(RST));  // open: carry
  D_Flip_Flop d_ff_2 (.clk(CLk), .D(LoadCondRead), .Q(LoadCondRead_prime), .reset(or_14_out));  // open: Qn, preset, en
  or or_14 (or_14_out, RST, RSTLoadConRead2, CacheWrite, RSTLoadConRead);
  and and_7 (INIT, PC_0, ON, not_1_out);

  assign LValid = LoadCache;
  assign LValidInst = LoadInstCache;
  assign RST_2 = RST;

  // Other names for the same wires on the sheet: LoSPin = LoSP; RamUse1 = CInc; RamAddS1 = RamWrite;
  //   RamUse2 = RamWrite; RamUse3 = RamAddS2; LoadCond5 = LoadInstCache; RamUse4 = LoadInstCache;
  //   LoadCond3 = LoadCache; RamAddS3 = LoadCache; RamUse5 = LoadCache; RR = RamRead; RSTLoadConRead1 = CacheWrite;
  //   WR = WriteRam
endmodule

module RamDecoder (
  input  [31:0] BRUTE_RAMADD,
  output [3:0] RAM_MASK,
  output [1:0] RAM_IN_SEL,
  output [15:0] RAM_ADD_REAL
);

  wire not_1_out, not_2_out, not_3_out, not_4_out;

  // Probe on BRUTE_RAMADD[19:4]
  // Probe on BRUTE_RAMADD
  // Probe on BRUTE_RAMADD[3:2]
  not not_1 (not_1_out, BRUTE_RAMADD[2]);
  not not_2 (not_2_out, BRUTE_RAMADD[3]);
  not not_3 (not_3_out, BRUTE_RAMADD[3]);
  not not_4 (not_4_out, BRUTE_RAMADD[2]);
  and and_1 (RAM_MASK[3], BRUTE_RAMADD[3], BRUTE_RAMADD[2]);
  and and_2 (RAM_MASK[2], BRUTE_RAMADD[3], not_1_out);
  and and_3 (RAM_MASK[1], not_2_out, BRUTE_RAMADD[2]);
  and and_4 (RAM_MASK[0], not_3_out, not_4_out);

  assign RAM_ADD_REAL = BRUTE_RAMADD[19:4];
  assign RAM_IN_SEL = BRUTE_RAMADD[3:2];

  // Other names for the same wires on the sheet: RAM_ADD_prime[31:0] = BRUTE_RAMADD; bank[1:0] = BRUTE_RAMADD[3:2];
  //   block[15:0] = BRUTE_RAMADD[19:4]
endmodule

module RAM_TRANSLATE (
  input  [31:0] RAM_IN,
  output [31:0] TRANSLATED
);


  assign TRANSLATED = {RAM_IN[7:0], RAM_IN[15:8], RAM_IN[23:16], RAM_IN[31:24]};
endmodule

module ALUDECI (
  input  b5,
  input  b3,
  input  b2,
  input  b1,
  input  b0,
  output a2,
  output a1,
  output a0
);

  wire and_2_out, and_3_out, and_4_out, and_5_out, and_6_out, not_1_out, not_2_out, not_3_out, not_4_out,
       not_5_out, not_6_out, not_7_out;

  not not_1 (not_1_out, b5);
  not not_2 (not_2_out, b5);
  not not_3 (not_3_out, b2);
  not not_4 (not_4_out, b1);
  not not_5 (not_5_out, b3);
  not not_6 (not_6_out, b1);
  not not_7 (not_7_out, b5);
  and and_1 (a2, not_1_out, b3, b1);
  and and_2 (and_2_out, not_2_out, not_3_out, b1);
  and and_3 (and_3_out, b3, b2, not_4_out);
  and and_4 (and_4_out, not_5_out, not_6_out);
  and and_5 (and_5_out, not_7_out, b0);
  and and_6 (and_6_out, b2, b1);
  or or_1 (a1, and_2_out, and_3_out);
  or or_2 (a0, and_4_out, and_5_out, and_6_out);
endmodule

module mask (
  input  b1,
  input  b0,
  output m3,
  output m2,
  output m1,
  output m0
);

  wire not_1_out, not_2_out, not_3_out, not_4_out;

  and and_1 (m3, b1, b0);
  not not_1 (not_1_out, b0);
  not not_2 (not_2_out, b1);
  not not_3 (not_3_out, b1);
  not not_4 (not_4_out, b0);
  and and_2 (m2, b1, not_1_out);
  and and_3 (m1, not_2_out, b0);
  and and_4 (m0, not_3_out, not_4_out);
endmodule

module InstructionCache (
  input  [31:0] PC,
  input  Clock,
  input  RESET,
  input  [31:0] MemoryData0,
  input  [31:0] MemoryData1,
  input  [31:0] MemoryData2,
  input  [31:0] MemoryData3,
  input  RW,
  input  Valided,
  input  [31:0] DataWrite,
  input  RamWrite,
  input  [31:0] RamAdress,
  output HIT,
  output [31:0] SetData,
  output isValid
);

  wire comparator_1_eq, comparator_2_eq, isV0, isV1, isV2, isV3, isV4, isV5, isV6, isV7, RSL0, RSL1, RSL2,
       RSL3, RSL4, RSL5, RSL6, SL0, SL1, SL2, SL3, SL4, SL5, SL6, SL7, SwL0, SwL1, SwL2, SwL3, SwL4, SwL5,
       SwL6, SwL7, V0, V1, V2, V3, V4, V5, V6, V7;
  wire [24:0] multiplexer_1_out, multiplexer_4_out, T0, T1, T2, T3, T4, T5, T6, T7;
  wire [31:0] S0, S1, S2, S3, S4, S5, S6, S7;

  CacheSet u_S0 (
    .Tag(PC[31:7]), .BlockSelect(PC[3:2]), .Clock(Clock), .Reset(RESET), .Load(SL0), .Loadw(RamWrite),
    .Dataw(DataWrite), .Data0(MemoryData0), .Data1(MemoryData1), .Data2(MemoryData2), .Data3(MemoryData3),
    .Valided(V0), .CanWrite(HIT), .DataOut(S0), .DataOut_2(T0), .isValid(isV0));
  CacheSet u_S4 (
    .Tag(PC[31:7]), .BlockSelect(PC[3:2]), .Clock(Clock), .Reset(RESET), .Load(SL4), .Loadw(RamWrite),
    .Dataw(DataWrite), .Data0(MemoryData0), .Data1(MemoryData1), .Data2(MemoryData2), .Data3(MemoryData3),
    .Valided(V4), .CanWrite(HIT), .DataOut(S4), .DataOut_2(T4), .isValid(isV4));
  Multiplexer #(.select(3), .width(25)) multiplexer_1 (
    .in0(T0), .in1(T1), .in2(T2), .in3(T3), .in4(T4), .in5(T5), .in6(T6), .in7(T7), .out(multiplexer_1_out),
    .sel(PC[6:4]));  // open: en
  Multiplexer #(.select(3), .width(32)) multiplexer_2 (
    .in0(S0), .in1(S1), .in2(S2), .in3(S3), .in4(S4), .in5(S5), .in6(S6), .in7(S7), .out(SetData),
    .sel(PC[6:4]));  // open: en
  Multiplexer #(.select(3)) multiplexer_3 (
    .in0(isV0), .in1(isV1), .in2(isV2), .in3(isV3), .in4(isV4), .in5(isV5), .in6(isV6), .in7(isV7),
    .out(isValid), .sel(PC[6:4]));  // open: en
  Multiplexer #(.select(3), .width(25)) multiplexer_4 (
    .in0(T0), .in1(T1), .in2(T2), .in3(T3), .in4(T4), .in5(T5), .in6(T6), .in7(T7), .out(multiplexer_4_out),
    .sel(PC[6:4]));  // open: en
  Multiplexer #(.select(3), .width(32)) multiplexer_5 (
    .in0(S0), .in1(S1), .in2(S2), .in3(S3), .in4(S4), .in5(S5), .in6(S6), .in7(S7), .out(SetData),
    .sel(PC[6:4]));  // open: en
  Multiplexer #(.select(3)) multiplexer_6 (
    .in0(isV0), .in1(isV1), .in2(isV2), .in3(isV3), .in4(isV4), .in5(isV5), .in6(isV6), .in7(isV7),
    .out(isValid), .sel(PC[6:4]));  // open: en
  Comparator #(.width(25)) comparator_1 (.a(multiplexer_1_out), .b(PC[31:7]), .eq(comparator_1_eq));  // open: gt, lt
  Comparator #(.width(25)) comparator_2 (.a(multiplexer_4_out), .b(PC[31:7]), .eq(comparator_2_eq));  // open: gt, lt
  and and_1 (HIT, comparator_1_eq, isValid);
  and and_2 (HIT, comparator_2_eq, isValid);
  CacheSet u_S1 (
    .Tag(PC[31:7]), .BlockSelect(PC[3:2]), .Clock(Clock), .Reset(RESET), .Load(SL1), .Loadw(RamWrite),
    .Dataw(DataWrite), .Data0(MemoryData0), .Data1(MemoryData1), .Data2(MemoryData2), .Data3(MemoryData3),
    .Valided(V1), .CanWrite(HIT), .DataOut(S1), .DataOut_2(T1), .isValid(isV1));
  CacheSet u_S5 (
    .Tag(PC[31:7]), .BlockSelect(PC[3:2]), .Clock(Clock), .Reset(RESET), .Load(SL5), .Loadw(RamWrite),
    .Dataw(DataWrite), .Data0(MemoryData0), .Data1(MemoryData1), .Data2(MemoryData2), .Data3(MemoryData3),
    .Valided(V5), .CanWrite(HIT), .DataOut(S5), .DataOut_2(T5), .isValid(isV5));
  CacheSet u_S2 (
    .Tag(PC[31:7]), .BlockSelect(PC[3:2]), .Clock(Clock), .Reset(RESET), .Load(SL2), .Loadw(RamWrite),
    .Dataw(DataWrite), .Data0(MemoryData0), .Data1(MemoryData1), .Data2(MemoryData2), .Data3(MemoryData3),
    .Valided(V2), .CanWrite(HIT), .DataOut(S2), .DataOut_2(T2), .isValid(isV2));
  CacheSet u_S6 (
    .Tag(PC[31:7]), .BlockSelect(PC[3:2]), .Clock(Clock), .Reset(RESET), .Load(SL6), .Loadw(RamWrite),
    .Dataw(DataWrite), .Data0(MemoryData0), .Data1(MemoryData1), .Data2(MemoryData2), .Data3(MemoryData3),
    .Valided(V6), .CanWrite(HIT), .DataOut(S6), .DataOut_2(T6), .isValid(isV6));
  Demultiplexer #(.select(3)) demultiplexer_1 (
    .out0(SL0), .out1(SL1), .out2(SL2), .out3(SL3), .out4(SL4), .out5(SL5), .out6(SL6), .out7(SL7), .in(RW),
    .sel(PC[6:4]));  // open: en
  Demultiplexer #(.select(3)) demultiplexer_2 (
    .out0(V0), .out1(V1), .out2(V2), .out3(V3), .out4(V4), .out5(V5), .out6(V6), .out7(V7), .in(Valided),
    .sel(PC[6:4]));  // open: en
  Demultiplexer #(.select(3)) demultiplexer_3 (
    .out0(SwL0), .out1(SwL1), .out2(SwL2), .out3(SwL3), .out4(SwL4), .out5(SwL5), .out6(SwL6), .out7(SwL7),
    .in(RamWrite), .sel(PC[6:4]));  // open: en
  Demultiplexer #(.select(3)) demultiplexer_4 (
    .out0(RSL0), .out1(RSL1), .out2(RSL2), .out3(RSL3), .out4(RSL4), .out5(RSL5), .out6(RSL6), .out7(SL7),
    .in(RamWrite), .sel(RamAdress[6:4]));  // open: en
  Demultiplexer #(.select(3)) demultiplexer_5 (
    .out0(V0), .out1(V1), .out2(V2), .out3(V3), .out4(V4), .out5(V5), .out6(V6), .out7(V7), .in(Valided),
    .sel(PC[6:4]));  // open: en
  Demultiplexer #(.select(3)) demultiplexer_6 (
    .out0(SwL0), .out1(SwL1), .out2(SwL2), .out3(SwL3), .out4(SwL4), .out5(SwL5), .out6(SwL6), .out7(SwL7),
    .in(RamWrite), .sel(PC[6:4]));  // open: en
  CacheSet u_S3 (
    .Tag(PC[31:7]), .BlockSelect(PC[3:2]), .Clock(Clock), .Reset(RESET), .Load(SL3), .Loadw(RamWrite),
    .Dataw(DataWrite), .Data0(MemoryData0), .Data1(MemoryData1), .Data2(MemoryData2), .Data3(MemoryData3),
    .Valided(V3), .CanWrite(HIT), .DataOut(S3), .DataOut_2(T3), .isValid(isV3));
  CacheSet u_S7 (
    .Tag(PC[31:7]), .BlockSelect(PC[3:2]), .Clock(Clock), .Reset(RESET), .Load(SL7), .Loadw(RamWrite),
    .Dataw(DataWrite), .Data0(MemoryData0), .Data1(MemoryData1), .Data2(MemoryData2), .Data3(MemoryData3),
    .Valided(V7), .CanWrite(HIT), .DataOut(S7), .DataOut_2(T7), .isValid(isV7));

  // Other names for the same wires on the sheet: Adress[31:0] = PC; ABlock[1:0] = PC[3:2]; ASet[2:0] = PC[6:4];
  //   ATag[24:0] = PC[31:7]; Data0[31:0] = MemoryData0; Data1[31:0] = MemoryData1; Data2[31:0] = MemoryData2;
  //   Data3[31:0] = MemoryData3; R_W = RW; RBlock[1:0] = RamAdress[3:2]; RSet[2:0] = RamAdress[6:4];
  //   RTag[24:0] = RamAdress[31:7]; SD[31:0] = SetData
endmodule

module InstructBank (
  input  [24:0] Tag,
  input  [1:0] BlockSelect,
  input  Clock,
  input  Reset,
  input  Load,
  input  Loadw,
  input  [31:0] Dataw,
  input  [31:0] Data0,
  input  [31:0] Data1,
  input  [31:0] Data2,
  input  [31:0] Data3,
  input  Valided,
  input  CanWrite,
  output [31:0] DataOut,
  output [24:0] DataOut_2,
  output isValid
);

  wire and_1_out, and_2_out, and_3_out, and_4_out, Load0, Load1, Load2, Load3;
  wire [31:0] B0, B1, B2, B3, Data0_t, Data1_t, Data2_t, Data3_t;

  Register #(.width(25)) u_Tag (.D(Tag), .en(Load), .Q(DataOut_2), .clk(Clock), .clr(Reset));
  Multiplexer #(.select(2), .width(32)) multiplexer_1 (
    .in0(B0), .in1(B1), .in2(B2), .in3(B3), .out(DataOut), .sel(BlockSelect));  // open: en
  D_Flip_Flop #(.trigger("falling")) d_ff_1 (
    .clk(Clock), .D(Valided), .Q(isValid), .en(Valided), .reset(Reset));  // open: Qn, preset
  and and_1 (and_1_out, Loadw, ~BlockSelect[0], BlockSelect[1], CanWrite);  // AND_Gate
  and and_2 (and_2_out, Loadw, BlockSelect[0], BlockSelect[1], CanWrite);
  or or_1 (Load0, Load, and_3_out);
  and and_3 (and_3_out, Loadw, ~BlockSelect[0], ~BlockSelect[1], CanWrite);  // AND_Gate
  or or_2 (Load1, Load, and_4_out);
  and and_4 (and_4_out, Loadw, BlockSelect[0], ~BlockSelect[1], CanWrite);  // AND_Gate
  or or_3 (Load2, Load, and_1_out);
  or or_4 (Load3, Load, and_2_out);
  Register #(.width(32)) u_B0 (.D(Data0_t), .en(Load0), .Q(B0), .clk(Clock), .clr(Reset));
  Register #(.width(32)) u_B1 (.D(Data1_t), .en(Load2), .Q(B1), .clk(Clock), .clr(Reset));
  Multiplexer #(.width(32)) multiplexer_2 (.in0(Data0), .in1(Dataw), .out(Data0_t), .sel(Loadw));  // open: en
  Multiplexer #(.width(32)) multiplexer_3 (.in0(Data1), .in1(Dataw), .out(Data1_t), .sel(Loadw));  // open: en
  Register #(.width(32)) u_B2 (.D(Data2_t), .en(Load1), .Q(B2), .clk(Clock), .clr(Reset));
  Register #(.width(32)) u_B3 (.D(Data3_t), .en(Load3), .Q(B3), .clk(Clock), .clr(Reset));
  Multiplexer #(.width(32)) multiplexer_4 (.in0(Data2), .in1(Dataw), .out(Data2_t), .sel(Loadw));  // open: en
  Multiplexer #(.width(32)) multiplexer_5 (.in0(Data3), .in1(Dataw), .out(Data3_t), .sel(Loadw));  // open: en

  // Other names for the same wires on the sheet: ATag[24:0] = Tag; BS[1:0] = BlockSelect; BS0 = BlockSelect[0];
  //   BS1 = BlockSelect[1]; Data0in[31:0] = Data0; Data1in[31:0] = Data1; Data2in[31:0] = Data2;
  //   Data3in[31:0] = Data3; Tag_t[24:0] = DataOut_2
endmodule

module ramuinew (
  input  HIT,
  input  RamRead,
  input  WriteRam,
  input  CLk,
  input  LoPCin,
  input  LoRegin,
  input  LoSP,
  input  [3:0] RRT,
  input  [3:0] WRT,
  input  RST,
  input  HitInsCache,
  input  isValid,
  input  isValidInst,
  input  [31:0] PC,
  input  ON,
  input  RST_2,
  output LoadCache,
  output LoadInstCache,
  output RamAddS,
  output RamUse,
  output RamWrite,
  output LValid,
  output LValidInst,
  output CacheWrite,
  output LoPC,
  output LoReg,
  output LoSP_2
);

  wire C_0, CInc, demultiplexer_1_out0, demultiplexer_1_out1, demultiplexer_2_out0, demultiplexer_3_out1,
       demultiplexer_5_out0, demultiplexer_6_out0, demultiplexer_7_out0, HIT_t, HitInsCache_t, IDLE_q, INIT,
       LoadCond, LoadCond1, LoadCond2, LoadCond4, LoadCondNR, LoadCondRead, LoadCondRead_prime, not_2_out,
       or_1_out, or_3_out, PC_0, RamAddS2, RamUse1, RorW, WHILE_2_q, WHILE_3_q, WHILE_q;
  wire [3:0] c_q, Count, InC;

  Comparator #(.width(32)) comparator_1 (.a(PC), .b({32{1'b0}}), .eq(PC_0));  // open: gt, lt
  or or_1 (or_1_out, INIT, LoadCond1, LoadCond4, LoadCond2, LoadCache, LoadInstCache);
  or or_2 (RamAddS, RamWrite, RamAddS2);
  and and_1 (LoPC, LoPCin, LoadCond);
  and and_2 (LoReg, LoRegin, LoadCond);
  and and_3 (LoSP_2, LoSP, LoadCond);
  and and_4 (HIT_t, HIT, isValid);
  and and_5 (HitInsCache_t, HitInsCache, isValidInst);
  Demultiplexer demultiplexer_1 (
    .out0(demultiplexer_1_out0), .out1(demultiplexer_1_out1), .in(IDLE_q), .sel(RorW));  // open: en
  D_Flip_Flop IDLE (.clk(CLk), .D(or_1_out), .Q(IDLE_q), .preset(RST));  // open: Qn, en, reset
  not not_1 (CInc, IDLE_q);
  or or_3 (or_3_out, demultiplexer_2_out0, RamUse1);
  Demultiplexer demultiplexer_2 (
    .out0(demultiplexer_2_out0), .out1(LoadCond4), .in(demultiplexer_1_out0), .sel(HitInsCache_t));  // open: en
  Demultiplexer demultiplexer_3 (
    .out0(CacheWrite), .out1(demultiplexer_3_out1), .in(demultiplexer_1_out1), .sel(RamRead));  // open: en
  Demultiplexer demultiplexer_4 (.out0(RamUse1), .out1(LoadInstCache), .in(WHILE_q), .sel(C_0));  // open: en
  D_Flip_Flop WHILE (.clk(CLk), .D(or_3_out), .Q(WHILE_q), .reset(RST));  // open: Qn, preset, en
  or or_4 (RamWrite, CacheWrite, demultiplexer_6_out0);
  Demultiplexer demultiplexer_5 (
    .out0(demultiplexer_5_out0), .out1(LoadCond2), .in(demultiplexer_3_out1), .sel(HIT_t));  // open: en
  Multiplexer #(.width(4)) multiplexer_1 (.in0(WRT), .in1(RRT), .out(InC), .sel(RamRead));  // open: en
  D_Flip_Flop WHILE_2 (.clk(CLk), .D(RamWrite), .Q(WHILE_2_q), .reset(RST));  // open: Qn, preset, en
  or or_5 (RamAddS2, demultiplexer_5_out0, demultiplexer_7_out0);
  // Probe on InC
  or or_6 (RorW, WriteRam, RamRead);
  Comparator #(.width(4), .mode("unsigned")) comparator_2 (.a(Count), .b(4'b0000), .eq(C_0));  // open: gt, lt
  or or_7 (LoadCondNR, LoadCond1, LoadCond2, LoadCond4);
  or or_8 (LoadCondRead, LoadCache, LoadInstCache);
  Demultiplexer demultiplexer_6 (.out0(demultiplexer_6_out0), .out1(LoadCond1), .in(WHILE_2_q), .sel(C_0));  // open: en
  D_Flip_Flop WHILE_3 (.clk(CLk), .D(RamAddS2), .Q(WHILE_3_q), .reset(RST));  // open: Qn, preset, en
  Demultiplexer demultiplexer_7 (.out0(demultiplexer_7_out0), .out1(LoadCache), .in(WHILE_3_q), .sel(C_0));  // open: en
  or or_9 (RamUse, RamAddS2, RamWrite, RamUse1, LoadInstCache, LoadCache);
  or or_10 (LValid, LoadCond1, LoadCache);
  or or_11 (LoadCond, LoadCondNR, LoadCondRead_prime);
  Counter #(.width(4), .max('hf)) c (.load(1'b1), .D(InC), .count(CInc), .Q(c_q), .clk(CLk), .clr(RST));  // open: carry
  D_Flip_Flop d_ff_1 (.clk(CLk), .D(LoadCondRead), .Q(LoadCondRead_prime), .reset(RST));  // open: Qn, preset, en
  and and_6 (INIT, PC_0, ON, not_2_out);
  not not_2 (not_2_out, RamUse);
  Adder #(.width(4)) adder_1 (.a(c_q), .b(4'b0001), .out(Count));  // open: cin, cout

  assign LValidInst = LoadInstCache;
  assign RST_2 = RST;

  // Other names for the same wires on the sheet: LValid0 = LoadCond1; LoSPin = LoSP; RamAddS1 = RamWrite;
  //   RamUse2 = RamWrite; RamUse3 = RamAddS2; LoadCond5 = LoadInstCache; RamUse4 = LoadInstCache;
  //   LoadCond3 = LoadCache; LValid1 = LoadCache; RamUse5 = LoadCache; RR = RamRead; WR = WriteRam
endmodule
